// Logisim project 8BitGates.circ as structural Verilog: 12 circuits, main circuit ALU
module ALU (
);

  _8_bit_Shift_Left u_8_bit_shift_left_1 ();  // open: shift_out, o, i, shift_in
  _8_bit_Shift_Right u_8_bit_shift_right_1 ();  // open: shift_out, o, i, shift_in
endmodule

module _8_bit_Shift_Right (
  input  shift_in,
  input  [7:0] i,
  output [7:0] o,
  output shift_out
);


  assign o = {shift_in, i[7:1]};
  assign shift_out = i[0];
endmodule

module _8_bit_Shift_Left (
  input  [7:0] i,
  input  shift_in,
  output shift_out,
  output [7:0] o
);


  assign o = {i[6:0], shift_in};
  assign shift_out = i[7];
endmodule

module _8_bit_Inverter (
  input  [7:0] in_1,
  output [7:0] out_2
);

  not not_1 (out_2[7], in_1[7]);
  not not_2 (out_2[6], in_1[6]);
  not not_3 (out_2[5], in_1[5]);
  not not_4 (out_2[4], in_1[4]);
  not not_5 (out_2[3], in_1[3]);
  not not_6 (out_2[2], in_1[2]);
  not not_7 (out_2[1], in_1[1]);
  not not_8 (out_2[0], in_1[0]);
endmodule

module _8_bit_And (
  input  [7:0] in_1,
  input  [7:0] in_2,
  output [7:0] out_3
);

  and and_1 (out_3[7], in_1[7], in_2[7]);
  and and_2 (out_3[6], in_1[6], in_2[6]);
  and and_3 (out_3[5], in_1[5], in_2[5]);
  and and_4 (out_3[4], in_1[4], in_2[4]);
  and and_5 (out_3[3], in_1[3], in_2[3]);
  and and_6 (out_3[2], in_1[2], in_2[2]);
  and and_7 (out_3[1], in_1[1], in_2[1]);
  and and_8 (out_3[0], in_1[0], in_2[0]);
endmodule

module _8_bit_Or (
  input  [7:0] in_1,
  input  [7:0] in_2,
  output [7:0] out_3
);

  or or_1 (out_3[7], in_1[7], in_2[7]);
  or or_2 (out_3[6], in_1[6], in_2[6]);
  or or_3 (out_3[5], in_1[5], in_2[5]);
  or or_4 (out_3[4], in_1[4], in_2[4]);
  or or_5 (out_3[3], in_1[3], in_2[3]);
  or or_6 (out_3[2], in_1[2], in_2[2]);
  or or_7 (out_3[1], in_1[1], in_2[1]);
  or or_8 (out_3[0], in_1[0], in_2[0]);
endmodule

module _8_bit_Xor (
  input  [7:0] in_1,
  input  [7:0] in_2,
  output [7:0] out_3
);

  xor xor_1 (out_3[7], in_1[7], in_2[7]);
  xor xor_2 (out_3[6], in_1[6], in_2[6]);
  xor xor_3 (out_3[5], in_1[5], in_2[5]);
  xor xor_4 (out_3[4], in_1[4], in_2[4]);
  xor xor_5 (out_3[3], in_1[3], in_2[3]);
  xor xor_6 (out_3[2], in_1[2], in_2[2]);
  xor xor_7 (out_3[1], in_1[1], in_2[1]);
  xor xor_8 (out_3[0], in_1[0], in_2[0]);
endmodule

module _1_bit_Adder (
  input  a,
  input  b,
  input  carry_in,
  output sum,
  output carry_out
);

  wire and_1_out, and_2_out, xor_1_out;

  xor xor_1 (xor_1_out, a, b);
  and and_1 (and_1_out, carry_in, xor_1_out);
  and and_2 (and_2_out, a, b);
  xor xor_2 (sum, xor_1_out, carry_in);
  or or_1 (carry_out, and_1_out, and_2_out);
endmodule

module _8_bit_Adder (
  input  [7:0] a,
  input  [7:0] b,
  input  carry_in,
  output carry_out,
  output [7:0] sum
);

  wire n1_bit_adder_2_carry_out, n1_bit_adder_3_carry_out, n1_bit_adder_4_carry_out,
       n1_bit_adder_5_carry_out, n1_bit_adder_6_carry_out, n1_bit_adder_7_carry_out, n1_bit_adder_8_carry_out;

  _1_bit_Adder u_1_bit_adder_1 (
    .sum(sum[7]), .carry_out(carry_out), .b(b[7]), .carry_in(n1_bit_adder_2_carry_out), .a(a[7]));
  _1_bit_Adder u_1_bit_adder_2 (
    .sum(sum[6]), .carry_out(n1_bit_adder_2_carry_out), .b(b[6]), .carry_in(n1_bit_adder_3_carry_out),
    .a(a[6]));
  _1_bit_Adder u_1_bit_adder_3 (
    .sum(sum[5]), .carry_out(n1_bit_adder_3_carry_out), .b(b[5]), .carry_in(n1_bit_adder_4_carry_out),
    .a(a[5]));
  _1_bit_Adder u_1_bit_adder_4 (
    .sum(sum[4]), .carry_out(n1_bit_adder_4_carry_out), .b(b[4]), .carry_in(n1_bit_adder_5_carry_out),
    .a(a[4]));
  _1_bit_Adder u_1_bit_adder_5 (
    .sum(sum[3]), .carry_out(n1_bit_adder_5_carry_out), .b(b[3]), .carry_in(n1_bit_adder_6_carry_out),
    .a(a[3]));
  _1_bit_Adder u_1_bit_adder_6 (
    .sum(sum[2]), .carry_out(n1_bit_adder_6_carry_out), .b(b[2]), .carry_in(n1_bit_adder_7_carry_out),
    .a(a[2]));
  _1_bit_Adder u_1_bit_adder_7 (
    .sum(sum[1]), .carry_out(n1_bit_adder_7_carry_out), .b(b[1]), .carry_in(n1_bit_adder_8_carry_out),
    .a(a[1]));
  _1_bit_Adder u_1_bit_adder_8 (
    .sum(sum[0]), .carry_out(n1_bit_adder_8_carry_out), .b(b[0]), .carry_in(carry_in), .a(a[0]));
endmodule

module _1_bit_Compare (
  input  all_bits_above_are_equal,
  input  a_larger,
  input  a,
  input  b,
  output out_5,
  output all_bits_equal_so_far,
  output a_larger_2
);

  wire and_2_out, not_1_out;

  xor xor_1 (out_5, a, b);
  not not_1 (not_1_out, out_5);
  and and_1 (all_bits_equal_so_far, not_1_out, all_bits_above_are_equal);
  and and_2 (and_2_out, all_bits_above_are_equal, a, out_5);
  or or_1 (a_larger_2, and_2_out, a_larger);
endmodule

module _8_bit_Compare (
  input  [7:0] a,
  input  [7:0] b,
  output [7:0] c,
  output out_4,
  output out_5
);

  wire n1_bit_compare_1_a_larger_2, n1_bit_compare_1_all_bits_equal_so_far, n1_bit_compare_2_a_larger_2,
       n1_bit_compare_2_all_bits_equal_so_far, n1_bit_compare_3_a_larger_2,
       n1_bit_compare_3_all_bits_equal_so_far, n1_bit_compare_4_a_larger_2,
       n1_bit_compare_4_all_bits_equal_so_far, n1_bit_compare_5_a_larger_2,
       n1_bit_compare_5_all_bits_equal_so_far, n1_bit_compare_6_a_larger_2,
       n1_bit_compare_6_all_bits_equal_so_far, n1_bit_compare_7_a_larger_2,
       n1_bit_compare_7_all_bits_equal_so_far;

  _1_bit_Compare u_1_bit_compare_1 (
    .all_bits_equal_so_far(n1_bit_compare_1_all_bits_equal_so_far), .a_larger_2(n1_bit_compare_1_a_larger_2),
    .out_5(c[7]), .a(a[7]), .b(b[7]), .all_bits_above_are_equal(1'b1), .a_larger(1'b0));
  _1_bit_Compare u_1_bit_compare_2 (
    .all_bits_equal_so_far(n1_bit_compare_2_all_bits_equal_so_far), .a_larger_2(n1_bit_compare_2_a_larger_2),
    .out_5(c[6]), .a(a[6]), .b(b[6]), .all_bits_above_are_equal(n1_bit_compare_1_all_bits_equal_so_far),
    .a_larger(n1_bit_compare_1_a_larger_2));
  _1_bit_Compare u_1_bit_compare_3 (
    .all_bits_equal_so_far(n1_bit_compare_3_all_bits_equal_so_far), .a_larger_2(n1_bit_compare_3_a_larger_2),
    .out_5(c[5]), .a(a[5]), .b(b[5]), .all_bits_above_are_equal(n1_bit_compare_2_all_bits_equal_so_far),
    .a_larger(n1_bit_compare_2_a_larger_2));
  _1_bit_Compare u_1_bit_compare_4 (
    .all_bits_equal_so_far(n1_bit_compare_4_all_bits_equal_so_far), .a_larger_2(n1_bit_compare_4_a_larger_2),
    .out_5(c[4]), .a(a[4]), .b(b[4]), .all_bits_above_are_equal(n1_bit_compare_3_all_bits_equal_so_far),
    .a_larger(n1_bit_compare_3_a_larger_2));
  _1_bit_Compare u_1_bit_compare_5 (
    .all_bits_equal_so_far(n1_bit_compare_5_all_bits_equal_so_far), .a_larger_2(n1_bit_compare_5_a_larger_2),
    .out_5(c[3]), .a(a[3]), .b(b[3]), .all_bits_above_are_equal(n1_bit_compare_4_all_bits_equal_so_far),
    .a_larger(n1_bit_compare_4_a_larger_2));
  _1_bit_Compare u_1_bit_compare_6 (
    .all_bits_equal_so_far(n1_bit_compare_6_all_bits_equal_so_far), .a_larger_2(n1_bit_compare_6_a_larger_2),
    .out_5(c[2]), .a(a[2]), .b(b[2]), .all_bits_above_are_equal(n1_bit_compare_5_all_bits_equal_so_far),
    .a_larger(n1_bit_compare_5_a_larger_2));
  _1_bit_Compare u_1_bit_compare_7 (
    .all_bits_equal_so_far(n1_bit_compare_7_all_bits_equal_so_far), .a_larger_2(n1_bit_compare_7_a_larger_2),
    .out_5(c[1]), .a(a[1]), .b(b[1]), .all_bits_above_are_equal(n1_bit_compare_6_all_bits_equal_so_far),
    .a_larger(n1_bit_compare_6_a_larger_2));
  _1_bit_Compare u_1_bit_compare_8 (
    .all_bits_equal_so_far(out_4), .a_larger_2(out_5), .out_5(c[0]), .a(a[0]), .b(b[0]),
    .all_bits_above_are_equal(n1_bit_compare_7_all_bits_equal_so_far), .a_larger(n1_bit_compare_7_a_larger_2));
endmodule

module _8_bit_Zero (
  input  [7:0] bus_in,
  output zero
);

  wire or_1_out;

  or or_1 (or_1_out, bus_in[7], bus_in[6], bus_in[5], bus_in[4], bus_in[3], bus_in[2], bus_in[1], bus_in[0]);
  not not_1 (zero, or_1_out);
endmodule
