// Logisim project CPU.circ as structural Verilog
module _1_bit_m (
  input  i,
  input  s,
  output o
);

  wire _1_out, _2_out, _4_out;

  nand _1 (_1_out, i, s);
  nand _2 (_2_out, _1_out, s);
  nand _3 (o, _1_out, _4_out);
  nand _4 (_4_out, o, _2_out);
endmodule

module _8_bit_Register (
  input  i,
  input  i_2,
  input  i_3,
  input  i_4,
  input  i_5,
  input  i_6,
  input  i_7,
  input  i_8,
  input  s,
  input  e,
  output o,
  output o_2,
  output o_3,
  output o_4,
  output o_5,
  output o_6,
  output o_7,
  output o_8
);

  wire n8_bit_memory_1_o, n8_bit_memory_1_o_2, n8_bit_memory_1_o_3, n8_bit_memory_1_o_4, n8_bit_memory_1_o_5,
       n8_bit_memory_1_o_6, n8_bit_memory_1_o_7, n8_bit_memory_1_o_8;

  _8_bit_Memory u_8_bit_memory_1 (
    .o(n8_bit_memory_1_o), .o_2(n8_bit_memory_1_o_2), .o_3(n8_bit_memory_1_o_3), .o_4(n8_bit_memory_1_o_4),
    .o_5(n8_bit_memory_1_o_5), .o_6(n8_bit_memory_1_o_6), .o_7(n8_bit_memory_1_o_7),
    .o_8(n8_bit_memory_1_o_8), .i_2(i_2), .i_3(i_3), .i_4(i_4), .i_5(i_5), .i_6(i_6), .i_7(i_7), .i_8(i_8),
    .s(s), .i(i));
  _8_bit_Enabler u_8_bit_enabler_1 (
    .o_3(o_3), .o_4(o_4), .o_5(o_5), .o_6(o_6), .o_7(o_7), .o_8(o_8), .o(o), .o_2(o_2),
    .i_3(n8_bit_memory_1_o_3), .i_4(n8_bit_memory_1_o_4), .i_5(n8_bit_memory_1_o_5),
    .i_6(n8_bit_memory_1_o_6), .i_7(n8_bit_memory_1_o_7), .i(n8_bit_memory_1_o), .i_8(n8_bit_memory_1_o_8),
    .e(e), .i_2(n8_bit_memory_1_o_2));
endmodule

module _1_byte_Register (
  input  [7:0] i,
  input  s,
  input  e,
  output [7:0] o
);

  wire [7:0] n1_byte_memory_1_o;

  _1_byte_Memory u_1_byte_memory_1 (.o(n1_byte_memory_1_o), .i(i), .s(s));
  _1_byte_Enabler u_1_byte_enabler_1 (.o(o), .i(n1_byte_memory_1_o), .e(e));
endmodule

module test_Register (
  input  in_1,
  input  in_2,
  input  in_3,
  input  in_4,
  input  [7:0] in_5,
  output [7:0] out_6,
  output [7:0] out_7
);

  wire and_1_out, not_1_out, not_2_out;
  wire [7:0] controlled_buffer_1_out;

  not not_1 (not_1_out, in_4);
  not not_2 (not_2_out, in_3);
  and and_1 (and_1_out, not_1_out, not_2_out);
  assign controlled_buffer_1_out = and_1_out ? in_5 : 8'bz;  // Controlled_Buffer controlled_buffer_1
  _1_byte_Register u_1_byte_register_1 (.o(out_6));  // open: s, e, i
  assign controlled_buffer_1_out = in_3 ? out_6 : 8'bz;  // Controlled_Buffer controlled_buffer_2
  _1_byte_Register u_1_byte_register_2 (.o(out_7));  // open: s, e, i
  assign controlled_buffer_1_out = in_4 ? out_7 : 8'bz;  // Controlled_Buffer controlled_buffer_3
endmodule

module MAR_play (
  input  [7:0] i,
  input  sa,
  output out_3,
  output out_4,
  output out_5,
  output out_6,
  output out_7,
  output out_8,
  output out_9,
  output out_10
);

  wire [3:0] binairy_to_bcd_converter_1_p2, binairy_to_bcd_converter_1_p3, binairy_to_bcd_converter_1_p4;

  Hex_Digit_Display hex_digit_display_1 (.value(binairy_to_bcd_converter_1_p2));  // open: dp
  Hex_Digit_Display hex_digit_display_2 (.value(binairy_to_bcd_converter_1_p3));  // open: dp
  // Binairy_to_BCD_converter binairy_to_bcd_converter_1: pin names not known; wires that end beside it: {1'b0, i}, binairy_to_bcd_converter_1_p2, binairy_to_bcd_converter_1_p3, binairy_to_bcd_converter_1_p4
  _8_bit_Memory u_8_bit_memory_1 (
    .o(out_3), .o_2(out_4), .o_3(out_5), .o_4(out_6), .o_5(out_7), .o_6(out_8), .o_7(out_9), .o_8(out_10),
    .i_2(i[1]), .i_3(i[2]), .i_4(i[3]), .i_5(i[4]), .i_6(i[5]), .i_7(i[6]), .i_8(i[7]), .s(sa), .i(i[0]));
  Hex_Digit_Display hex_digit_display_3 (.value(binairy_to_bcd_converter_1_p4));  // open: dp
endmodule

module RAM_Register_play (
  input  [7:0] i,
  input  s,
  input  e,
  output [7:0] op,
  output [7:0] o
);

  _1_byte_Memory u_1_byte_memory_1 (.o(op), .i(i), .s(s));
  _1_byte_Enabler u_1_byte_enabler_1 (.o(o), .i(op), .e(e));
endmodule

module RAM_Register_Area_play (
  input  y,
  input  x,
  input  [7:0] bus_in,
  input  s,
  input  e,
  output [7:0] op,
  output [7:0] bus_out
);

  wire and_1_out, and_2_out, X_out;
  wire [7:0] ram_register_play_1_o;

  and u_X (X_out, x, y);
  LED led_1 (.in(X_out));
  and and_1 (and_1_out, X_out, s);
  and and_2 (and_2_out, X_out, e);
  RAM_Register_play ram_register_play_1 (.op(op), .o(ram_register_play_1_o), .i(bus_in), .s(and_1_out), .e(and_2_out));
  assign bus_out = and_2_out ? ram_register_play_1_o : 8'bz;  // Controlled_Buffer controlled_buffer_1
endmodule

module RAM_256_play (
  input  [7:0] Address,
  input  sa,
  input  s,
  input  e,
  input  [7:0] in,
  output [7:0] out_6,
  output [7:0] out_7,
  output [7:0] out_8,
  output [7:0] out_9,
  output [7:0] out_10,
  output [7:0] out_11,
  output [7:0] out_12,
  output [7:0] out_13,
  output [7:0] out_14,
  output [7:0] out_15,
  output [7:0] out_16,
  output [7:0] out_17,
  output [7:0] out_18,
  output [7:0] out_19,
  output [7:0] out_20,
  output [7:0] out_21,
  output [7:0] out,
  output [7:0] out_23,
  output [7:0] out_24,
  output [7:0] out_25,
  output [7:0] out_26,
  output [7:0] out_27,
  output [7:0] out_28,
  output [7:0] out_29,
  output [7:0] out_30,
  output [7:0] out_31,
  output [7:0] out_32,
  output [7:0] out_33,
  output [7:0] out_34,
  output [7:0] out_35,
  output [7:0] out_36,
  output [7:0] out_37,
  output [7:0] out_38,
  output [7:0] out_39,
  output [7:0] out_40,
  output [7:0] out_41,
  output [7:0] out_42,
  output [7:0] out_43,
  output [7:0] out_44,
  output [7:0] out_45,
  output [7:0] out_46,
  output [7:0] out_47,
  output [7:0] out_48,
  output [7:0] out_49,
  output [7:0] out_50,
  output [7:0] out_51,
  output [7:0] out_52,
  output [7:0] out_53,
  output [7:0] out_54,
  output [7:0] out_55,
  output [7:0] out_56,
  output [7:0] out_57,
  output [7:0] out_58,
  output [7:0] out_59,
  output [7:0] out_60,
  output [7:0] out_61,
  output [7:0] out_62,
  output [7:0] out_63,
  output [7:0] out_64,
  output [7:0] out_65,
  output [7:0] out_66,
  output [7:0] out_67,
  output [7:0] out_68,
  output [7:0] out_69,
  output [7:0] out_70,
  output [7:0] out_71,
  output [7:0] out_72,
  output [7:0] out_73,
  output [7:0] out_74,
  output [7:0] out_75,
  output [7:0] out_76,
  output [7:0] out_77,
  output [7:0] out_78,
  output [7:0] out_79,
  output [7:0] out_80,
  output [7:0] out_81,
  output [7:0] out_82,
  output [7:0] out_83,
  output [7:0] out_84,
  output [7:0] out_85,
  output [7:0] out_86,
  output [7:0] out_87,
  output [7:0] out_88,
  output [7:0] out_89,
  output [7:0] out_90,
  output [7:0] out_91,
  output [7:0] out_92,
  output [7:0] out_93,
  output [7:0] out_94,
  output [7:0] out_95,
  output [7:0] out_96,
  output [7:0] out_97,
  output [7:0] out_98,
  output [7:0] out_99,
  output [7:0] out_100,
  output [7:0] out_101,
  output [7:0] out_102,
  output [7:0] out_103,
  output [7:0] out_104,
  output [7:0] out_105,
  output [7:0] out_106,
  output [7:0] out_107,
  output [7:0] out_108,
  output [7:0] out_109,
  output [7:0] out_110,
  output [7:0] out_111,
  output [7:0] out_112,
  output [7:0] out_113,
  output [7:0] out_114,
  output [7:0] out_115,
  output [7:0] out_116,
  output [7:0] out_117,
  output [7:0] out_118,
  output [7:0] out_119,
  output [7:0] out_120,
  output [7:0] out_121,
  output [7:0] out_122,
  output [7:0] out_123,
  output [7:0] out_124,
  output [7:0] out_125,
  output [7:0] out_126,
  output [7:0] out_127,
  output [7:0] out_128,
  output [7:0] out_129,
  output [7:0] out_130,
  output [7:0] out_131,
  output [7:0] out_132,
  output [7:0] out_133,
  output [7:0] out_134,
  output [7:0] out_135,
  output [7:0] out_136,
  output [7:0] out_137,
  output [7:0] out_138,
  output [7:0] out_139,
  output [7:0] out_140,
  output [7:0] out_141,
  output [7:0] out_142,
  output [7:0] out_143,
  output [7:0] out_144,
  output [7:0] out_145,
  output [7:0] out_146,
  output [7:0] out_147,
  output [7:0] out_148,
  output [7:0] out_149,
  output [7:0] out_150,
  output [7:0] out_151,
  output [7:0] out_152,
  output [7:0] out_153,
  output [7:0] out_154,
  output [7:0] out_155,
  output [7:0] out_156,
  output [7:0] out_157,
  output [7:0] out_158,
  output [7:0] out_159,
  output [7:0] out_160,
  output [7:0] out_161,
  output [7:0] out_162,
  output [7:0] out_163,
  output [7:0] out_164,
  output [7:0] out_165,
  output [7:0] out_166,
  output [7:0] out_167,
  output [7:0] out_168,
  output [7:0] out_169,
  output [7:0] out_170,
  output [7:0] out_171,
  output [7:0] out_172,
  output [7:0] out_173,
  output [7:0] out_174,
  output [7:0] out_175,
  output [7:0] out_176,
  output [7:0] out_177,
  output [7:0] out_178,
  output [7:0] out_179,
  output [7:0] out_180,
  output [7:0] out_181,
  output [7:0] out_182,
  output [7:0] out_183,
  output [7:0] out_184,
  output [7:0] out_185,
  output [7:0] out_186,
  output [7:0] out_187,
  output [7:0] out_188,
  output [7:0] out_189,
  output [7:0] out_190,
  output [7:0] out_191,
  output [7:0] out_192,
  output [7:0] out_193,
  output [7:0] out_194,
  output [7:0] out_195,
  output [7:0] out_196,
  output [7:0] out_197,
  output [7:0] out_198,
  output [7:0] out_199,
  output [7:0] out_200,
  output [7:0] out_201,
  output [7:0] out_202,
  output [7:0] out_203,
  output [7:0] out_204,
  output [7:0] out_205,
  output [7:0] out_206,
  output [7:0] out_207,
  output [7:0] out_208,
  output [7:0] out_209,
  output [7:0] out_210,
  output [7:0] out_211,
  output [7:0] out_212,
  output [7:0] out_213,
  output [7:0] out_214,
  output [7:0] out_215,
  output [7:0] out_216,
  output [7:0] out_217,
  output [7:0] out_218,
  output [7:0] out_219,
  output [7:0] out_220,
  output [7:0] out_221,
  output [7:0] out_222,
  output [7:0] out_223,
  output [7:0] out_224,
  output [7:0] out_225,
  output [7:0] out_226,
  output [7:0] out_227,
  output [7:0] out_228,
  output [7:0] out_229,
  output [7:0] out_230,
  output [7:0] out_231,
  output [7:0] out_232,
  output [7:0] out_233,
  output [7:0] out_234,
  output [7:0] out_235,
  output [7:0] out_236,
  output [7:0] out_237,
  output [7:0] out_238,
  output [7:0] out_239,
  output [7:0] out_240,
  output [7:0] out_241,
  output [7:0] out_242,
  output [7:0] out_243,
  output [7:0] out_244,
  output [7:0] out_245,
  output [7:0] out_246,
  output [7:0] out_247,
  output [7:0] out_248,
  output [7:0] out_249,
  output [7:0] out_250,
  output [7:0] out_251,
  output [7:0] out_252,
  output [7:0] out_253,
  output [7:0] out_254,
  output [7:0] out_255,
  output [7:0] out_256,
  output [7:0] out_257,
  output [7:0] out_258,
  output [7:0] out_259,
  output [7:0] out_260,
  output [7:0] out_261,
  output [7:0] out_262
);

  wire mar_play_1_out_3, mar_play_1_out_4, mar_play_1_out_5, mar_play_1_out_6, mar_play_1_out_7,
       mar_play_1_out_8, mar_play_1_out_9, mar_play_1_out_10, n4x16_decoder_1_out_5, n4x16_decoder_1_out_6,
       n4x16_decoder_1_out_7, n4x16_decoder_1_out_8, n4x16_decoder_1_out_9, n4x16_decoder_1_out_10,
       n4x16_decoder_1_out_11, n4x16_decoder_1_out_12, n4x16_decoder_1_out_13, n4x16_decoder_1_out_14,
       n4x16_decoder_1_out_15, n4x16_decoder_1_out_16, n4x16_decoder_1_out_17, n4x16_decoder_1_out_18,
       n4x16_decoder_1_out_19, n4x16_decoder_1_out_20, n4x16_decoder_2_out_5, n4x16_decoder_2_out_6,
       n4x16_decoder_2_out_7, n4x16_decoder_2_out_8, n4x16_decoder_2_out_9, n4x16_decoder_2_out_10,
       n4x16_decoder_2_out_11, n4x16_decoder_2_out_12, n4x16_decoder_2_out_13, n4x16_decoder_2_out_14,
       n4x16_decoder_2_out_15, n4x16_decoder_2_out_16, n4x16_decoder_2_out_17, n4x16_decoder_2_out_18,
       n4x16_decoder_2_out_19, n4x16_decoder_2_out_20;

  _4x16_Decoder u_4x16_decoder_1 (
    .out_20(n4x16_decoder_1_out_20), .out_5(n4x16_decoder_1_out_5), .out_6(n4x16_decoder_1_out_6),
    .out_7(n4x16_decoder_1_out_7), .out_8(n4x16_decoder_1_out_8), .out_9(n4x16_decoder_1_out_9),
    .out_10(n4x16_decoder_1_out_10), .out_11(n4x16_decoder_1_out_11), .out_12(n4x16_decoder_1_out_12),
    .out_13(n4x16_decoder_1_out_13), .out_14(n4x16_decoder_1_out_14), .out_15(n4x16_decoder_1_out_15),
    .out_16(n4x16_decoder_1_out_16), .out_17(n4x16_decoder_1_out_17), .out_18(n4x16_decoder_1_out_18),
    .out_19(n4x16_decoder_1_out_19), .d(mar_play_1_out_3), .a(mar_play_1_out_6), .b(mar_play_1_out_5),
    .c(mar_play_1_out_4));
  MAR_play mar_play_1 (
    .out_3(mar_play_1_out_3), .out_4(mar_play_1_out_4), .out_5(mar_play_1_out_5), .out_6(mar_play_1_out_6),
    .out_7(mar_play_1_out_7), .out_8(mar_play_1_out_8), .out_9(mar_play_1_out_9), .out_10(mar_play_1_out_10),
    .i(Address), .sa(sa));
  _4x16_Decoder u_4x16_decoder_2 (
    .out_20(n4x16_decoder_2_out_20), .out_5(n4x16_decoder_2_out_5), .out_6(n4x16_decoder_2_out_6),
    .out_7(n4x16_decoder_2_out_7), .out_8(n4x16_decoder_2_out_8), .out_9(n4x16_decoder_2_out_9),
    .out_10(n4x16_decoder_2_out_10), .out_11(n4x16_decoder_2_out_11), .out_12(n4x16_decoder_2_out_12),
    .out_13(n4x16_decoder_2_out_13), .out_14(n4x16_decoder_2_out_14), .out_15(n4x16_decoder_2_out_15),
    .out_16(n4x16_decoder_2_out_16), .out_17(n4x16_decoder_2_out_17), .out_18(n4x16_decoder_2_out_18),
    .out_19(n4x16_decoder_2_out_19), .d(mar_play_1_out_7), .a(mar_play_1_out_10), .b(mar_play_1_out_9),
    .c(mar_play_1_out_8));
  RAM_Register_Area_play ram_register_area_play_1 (
    .bus_out(out), .op(out_6), .x(n4x16_decoder_2_out_5), .bus_in(in), .s(s), .e(e), .y(n4x16_decoder_1_out_5));
  RAM_Register_Area_play ram_register_area_play_2 (
    .bus_out(out), .op(out_23), .x(n4x16_decoder_2_out_6), .bus_in(in), .s(s), .e(e),
    .y(n4x16_decoder_1_out_5));
  RAM_Register_Area_play ram_register_area_play_3 (
    .bus_out(out), .op(out_39), .x(n4x16_decoder_2_out_7), .bus_in(in), .s(s), .e(e),
    .y(n4x16_decoder_1_out_5));
  RAM_Register_Area_play ram_register_area_play_4 (
    .bus_out(out), .op(out_55), .x(n4x16_decoder_2_out_8), .bus_in(in), .s(s), .e(e),
    .y(n4x16_decoder_1_out_5));
  RAM_Register_Area_play ram_register_area_play_5 (
    .bus_out(out), .op(out_71), .x(n4x16_decoder_2_out_9), .bus_in(in), .s(s), .e(e),
    .y(n4x16_decoder_1_out_5));
  RAM_Register_Area_play ram_register_area_play_6 (
    .bus_out(out), .op(out_87), .x(n4x16_decoder_2_out_10), .bus_in(in), .s(s), .e(e),
    .y(n4x16_decoder_1_out_5));
  RAM_Register_Area_play ram_register_area_play_7 (
    .bus_out(out), .op(out_103), .x(n4x16_decoder_2_out_11), .bus_in(in), .s(s), .e(e),
    .y(n4x16_decoder_1_out_5));
  RAM_Register_Area_play ram_register_area_play_8 (
    .bus_out(out), .op(out_119), .x(n4x16_decoder_2_out_12), .bus_in(in), .s(s), .e(e),
    .y(n4x16_decoder_1_out_5));
  RAM_Register_Area_play ram_register_area_play_9 (
    .bus_out(out), .op(out_135), .x(n4x16_decoder_2_out_13), .bus_in(in), .s(s), .e(e),
    .y(n4x16_decoder_1_out_5));
  RAM_Register_Area_play ram_register_area_play_10 (
    .bus_out(out), .op(out_151), .x(n4x16_decoder_2_out_14), .bus_in(in), .s(s), .e(e),
    .y(n4x16_decoder_1_out_5));
  RAM_Register_Area_play ram_register_area_play_11 (
    .bus_out(out), .op(out_167), .x(n4x16_decoder_2_out_15), .bus_in(in), .s(s), .e(e),
    .y(n4x16_decoder_1_out_5));
  RAM_Register_Area_play ram_register_area_play_12 (
    .bus_out(out), .op(out_183), .x(n4x16_decoder_2_out_16), .bus_in(in), .s(s), .e(e),
    .y(n4x16_decoder_1_out_5));
  RAM_Register_Area_play ram_register_area_play_13 (
    .bus_out(out), .op(out_199), .x(n4x16_decoder_2_out_17), .bus_in(in), .s(s), .e(e),
    .y(n4x16_decoder_1_out_5));
  RAM_Register_Area_play ram_register_area_play_14 (
    .bus_out(out), .op(out_215), .x(n4x16_decoder_2_out_18), .bus_in(in), .s(s), .e(e),
    .y(n4x16_decoder_1_out_5));
  RAM_Register_Area_play ram_register_area_play_15 (
    .bus_out(out), .op(out_231), .x(n4x16_decoder_2_out_19), .bus_in(in), .s(s), .e(e),
    .y(n4x16_decoder_1_out_5));
  RAM_Register_Area_play ram_register_area_play_16 (
    .bus_out(out), .op(out_247), .x(n4x16_decoder_2_out_20), .bus_in(in), .s(s), .e(e),
    .y(n4x16_decoder_1_out_5));
  RAM_Register_Area_play ram_register_area_play_17 (
    .bus_out(out), .op(out_7), .x(n4x16_decoder_2_out_5), .bus_in(in), .s(s), .e(e), .y(n4x16_decoder_1_out_6));
  RAM_Register_Area_play ram_register_area_play_18 (
    .bus_out(out), .op(out_24), .x(n4x16_decoder_2_out_6), .bus_in(in), .s(s), .e(e),
    .y(n4x16_decoder_1_out_6));
  RAM_Register_Area_play ram_register_area_play_19 (
    .bus_out(out), .op(out_40), .x(n4x16_decoder_2_out_7), .bus_in(in), .s(s), .e(e),
    .y(n4x16_decoder_1_out_6));
  RAM_Register_Area_play ram_register_area_play_20 (
    .bus_out(out), .op(out_56), .x(n4x16_decoder_2_out_8), .bus_in(in), .s(s), .e(e),
    .y(n4x16_decoder_1_out_6));
  RAM_Register_Area_play ram_register_area_play_21 (
    .bus_out(out), .op(out_72), .x(n4x16_decoder_2_out_9), .bus_in(in), .s(s), .e(e),
    .y(n4x16_decoder_1_out_6));
  RAM_Register_Area_play ram_register_area_play_22 (
    .bus_out(out), .op(out_88), .x(n4x16_decoder_2_out_10), .bus_in(in), .s(s), .e(e),
    .y(n4x16_decoder_1_out_6));
  RAM_Register_Area_play ram_register_area_play_23 (
    .bus_out(out), .op(out_104), .x(n4x16_decoder_2_out_11), .bus_in(in), .s(s), .e(e),
    .y(n4x16_decoder_1_out_6));
  RAM_Register_Area_play ram_register_area_play_24 (
    .bus_out(out), .op(out_120), .x(n4x16_decoder_2_out_12), .bus_in(in), .s(s), .e(e),
    .y(n4x16_decoder_1_out_6));
  RAM_Register_Area_play ram_register_area_play_25 (
    .bus_out(out), .op(out_136), .x(n4x16_decoder_2_out_13), .bus_in(in), .s(s), .e(e),
    .y(n4x16_decoder_1_out_6));
  RAM_Register_Area_play ram_register_area_play_26 (
    .bus_out(out), .op(out_152), .x(n4x16_decoder_2_out_14), .bus_in(in), .s(s), .e(e),
    .y(n4x16_decoder_1_out_6));
  RAM_Register_Area_play ram_register_area_play_27 (
    .bus_out(out), .op(out_168), .x(n4x16_decoder_2_out_15), .bus_in(in), .s(s), .e(e),
    .y(n4x16_decoder_1_out_6));
  RAM_Register_Area_play ram_register_area_play_28 (
    .bus_out(out), .op(out_184), .x(n4x16_decoder_2_out_16), .bus_in(in), .s(s), .e(e),
    .y(n4x16_decoder_1_out_6));
  RAM_Register_Area_play ram_register_area_play_29 (
    .bus_out(out), .op(out_200), .x(n4x16_decoder_2_out_17), .bus_in(in), .s(s), .e(e),
    .y(n4x16_decoder_1_out_6));
  RAM_Register_Area_play ram_register_area_play_30 (
    .bus_out(out), .op(out_216), .x(n4x16_decoder_2_out_18), .bus_in(in), .s(s), .e(e),
    .y(n4x16_decoder_1_out_6));
  RAM_Register_Area_play ram_register_area_play_31 (
    .bus_out(out), .op(out_232), .x(n4x16_decoder_2_out_19), .bus_in(in), .s(s), .e(e),
    .y(n4x16_decoder_1_out_6));
  RAM_Register_Area_play ram_register_area_play_32 (
    .bus_out(out), .op(out_248), .x(n4x16_decoder_2_out_20), .bus_in(in), .s(s), .e(e),
    .y(n4x16_decoder_1_out_6));
  RAM_Register_Area_play ram_register_area_play_33 (
    .bus_out(out), .op(out_8), .x(n4x16_decoder_2_out_5), .bus_in(in), .s(s), .e(e), .y(n4x16_decoder_1_out_7));
  RAM_Register_Area_play ram_register_area_play_34 (
    .bus_out(out), .op(out_25), .x(n4x16_decoder_2_out_6), .bus_in(in), .s(s), .e(e),
    .y(n4x16_decoder_1_out_7));
  RAM_Register_Area_play ram_register_area_play_35 (
    .bus_out(out), .op(out_41), .x(n4x16_decoder_2_out_7), .bus_in(in), .s(s), .e(e),
    .y(n4x16_decoder_1_out_7));
  RAM_Register_Area_play ram_register_area_play_36 (
    .bus_out(out), .op(out_57), .x(n4x16_decoder_2_out_8), .bus_in(in), .s(s), .e(e),
    .y(n4x16_decoder_1_out_7));
  RAM_Register_Area_play ram_register_area_play_37 (
    .bus_out(out), .op(out_73), .x(n4x16_decoder_2_out_9), .bus_in(in), .s(s), .e(e),
    .y(n4x16_decoder_1_out_7));
  RAM_Register_Area_play ram_register_area_play_38 (
    .bus_out(out), .op(out_89), .x(n4x16_decoder_2_out_10), .bus_in(in), .s(s), .e(e),
    .y(n4x16_decoder_1_out_7));
  RAM_Register_Area_play ram_register_area_play_39 (
    .bus_out(out), .op(out_105), .x(n4x16_decoder_2_out_11), .bus_in(in), .s(s), .e(e),
    .y(n4x16_decoder_1_out_7));
  RAM_Register_Area_play ram_register_area_play_40 (
    .bus_out(out), .op(out_121), .x(n4x16_decoder_2_out_12), .bus_in(in), .s(s), .e(e),
    .y(n4x16_decoder_1_out_7));
  RAM_Register_Area_play ram_register_area_play_41 (
    .bus_out(out), .op(out_137), .x(n4x16_decoder_2_out_13), .bus_in(in), .s(s), .e(e),
    .y(n4x16_decoder_1_out_7));
  RAM_Register_Area_play ram_register_area_play_42 (
    .bus_out(out), .op(out_153), .x(n4x16_decoder_2_out_14), .bus_in(in), .s(s), .e(e),
    .y(n4x16_decoder_1_out_7));
  RAM_Register_Area_play ram_register_area_play_43 (
    .bus_out(out), .op(out_169), .x(n4x16_decoder_2_out_15), .bus_in(in), .s(s), .e(e),
    .y(n4x16_decoder_1_out_7));
  RAM_Register_Area_play ram_register_area_play_44 (
    .bus_out(out), .op(out_185), .x(n4x16_decoder_2_out_16), .bus_in(in), .s(s), .e(e),
    .y(n4x16_decoder_1_out_7));
  RAM_Register_Area_play ram_register_area_play_45 (
    .bus_out(out), .op(out_201), .x(n4x16_decoder_2_out_17), .bus_in(in), .s(s), .e(e),
    .y(n4x16_decoder_1_out_7));
  RAM_Register_Area_play ram_register_area_play_46 (
    .bus_out(out), .op(out_217), .x(n4x16_decoder_2_out_18), .bus_in(in), .s(s), .e(e),
    .y(n4x16_decoder_1_out_7));
  RAM_Register_Area_play ram_register_area_play_47 (
    .bus_out(out), .op(out_233), .x(n4x16_decoder_2_out_19), .bus_in(in), .s(s), .e(e),
    .y(n4x16_decoder_1_out_7));
  RAM_Register_Area_play ram_register_area_play_48 (
    .bus_out(out), .op(out_249), .x(n4x16_decoder_2_out_20), .bus_in(in), .s(s), .e(e),
    .y(n4x16_decoder_1_out_7));
  RAM_Register_Area_play ram_register_area_play_49 (
    .bus_out(out), .op(out_9), .x(n4x16_decoder_2_out_5), .bus_in(in), .s(s), .e(e), .y(n4x16_decoder_1_out_8));
  RAM_Register_Area_play ram_register_area_play_50 (
    .bus_out(out), .op(out_26), .x(n4x16_decoder_2_out_6), .bus_in(in), .s(s), .e(e),
    .y(n4x16_decoder_1_out_8));
  RAM_Register_Area_play ram_register_area_play_51 (
    .bus_out(out), .op(out_42), .x(n4x16_decoder_2_out_7), .bus_in(in), .s(s), .e(e),
    .y(n4x16_decoder_1_out_8));
  RAM_Register_Area_play ram_register_area_play_52 (
    .bus_out(out), .op(out_58), .x(n4x16_decoder_2_out_8), .bus_in(in), .s(s), .e(e),
    .y(n4x16_decoder_1_out_8));
  RAM_Register_Area_play ram_register_area_play_53 (
    .bus_out(out), .op(out_74), .x(n4x16_decoder_2_out_9), .bus_in(in), .s(s), .e(e),
    .y(n4x16_decoder_1_out_8));
  RAM_Register_Area_play ram_register_area_play_54 (
    .bus_out(out), .op(out_90), .x(n4x16_decoder_2_out_10), .bus_in(in), .s(s), .e(e),
    .y(n4x16_decoder_1_out_8));
  RAM_Register_Area_play ram_register_area_play_55 (
    .bus_out(out), .op(out_106), .x(n4x16_decoder_2_out_11), .bus_in(in), .s(s), .e(e),
    .y(n4x16_decoder_1_out_8));
  RAM_Register_Area_play ram_register_area_play_56 (
    .bus_out(out), .op(out_122), .x(n4x16_decoder_2_out_12), .bus_in(in), .s(s), .e(e),
    .y(n4x16_decoder_1_out_8));
  RAM_Register_Area_play ram_register_area_play_57 (
    .bus_out(out), .op(out_138), .x(n4x16_decoder_2_out_13), .bus_in(in), .s(s), .e(e),
    .y(n4x16_decoder_1_out_8));
  RAM_Register_Area_play ram_register_area_play_58 (
    .bus_out(out), .op(out_154), .x(n4x16_decoder_2_out_14), .bus_in(in), .s(s), .e(e),
    .y(n4x16_decoder_1_out_8));
  RAM_Register_Area_play ram_register_area_play_59 (
    .bus_out(out), .op(out_170), .x(n4x16_decoder_2_out_15), .bus_in(in), .s(s), .e(e),
    .y(n4x16_decoder_1_out_8));
  RAM_Register_Area_play ram_register_area_play_60 (
    .bus_out(out), .op(out_186), .x(n4x16_decoder_2_out_16), .bus_in(in), .s(s), .e(e),
    .y(n4x16_decoder_1_out_8));
  RAM_Register_Area_play ram_register_area_play_61 (
    .bus_out(out), .op(out_202), .x(n4x16_decoder_2_out_17), .bus_in(in), .s(s), .e(e),
    .y(n4x16_decoder_1_out_8));
  RAM_Register_Area_play ram_register_area_play_62 (
    .bus_out(out), .op(out_218), .x(n4x16_decoder_2_out_18), .bus_in(in), .s(s), .e(e),
    .y(n4x16_decoder_1_out_8));
  RAM_Register_Area_play ram_register_area_play_63 (
    .bus_out(out), .op(out_234), .x(n4x16_decoder_2_out_19), .bus_in(in), .s(s), .e(e),
    .y(n4x16_decoder_1_out_8));
  RAM_Register_Area_play ram_register_area_play_64 (
    .bus_out(out), .op(out_250), .x(n4x16_decoder_2_out_20), .bus_in(in), .s(s), .e(e),
    .y(n4x16_decoder_1_out_8));
  RAM_Register_Area_play ram_register_area_play_65 (
    .bus_out(out), .op(out_10), .x(n4x16_decoder_2_out_5), .bus_in(in), .s(s), .e(e),
    .y(n4x16_decoder_1_out_9));
  RAM_Register_Area_play ram_register_area_play_66 (
    .bus_out(out), .op(out_27), .x(n4x16_decoder_2_out_6), .bus_in(in), .s(s), .e(e),
    .y(n4x16_decoder_1_out_9));
  RAM_Register_Area_play ram_register_area_play_67 (
    .bus_out(out), .op(out_43), .x(n4x16_decoder_2_out_7), .bus_in(in), .s(s), .e(e),
    .y(n4x16_decoder_1_out_9));
  RAM_Register_Area_play ram_register_area_play_68 (
    .bus_out(out), .op(out_59), .x(n4x16_decoder_2_out_8), .bus_in(in), .s(s), .e(e),
    .y(n4x16_decoder_1_out_9));
  RAM_Register_Area_play ram_register_area_play_69 (
    .bus_out(out), .op(out_75), .x(n4x16_decoder_2_out_9), .bus_in(in), .s(s), .e(e),
    .y(n4x16_decoder_1_out_9));
  RAM_Register_Area_play ram_register_area_play_70 (
    .bus_out(out), .op(out_91), .x(n4x16_decoder_2_out_10), .bus_in(in), .s(s), .e(e),
    .y(n4x16_decoder_1_out_9));
  RAM_Register_Area_play ram_register_area_play_71 (
    .bus_out(out), .op(out_107), .x(n4x16_decoder_2_out_11), .bus_in(in), .s(s), .e(e),
    .y(n4x16_decoder_1_out_9));
  RAM_Register_Area_play ram_register_area_play_72 (
    .bus_out(out), .op(out_123), .x(n4x16_decoder_2_out_12), .bus_in(in), .s(s), .e(e),
    .y(n4x16_decoder_1_out_9));
  RAM_Register_Area_play ram_register_area_play_73 (
    .bus_out(out), .op(out_139), .x(n4x16_decoder_2_out_13), .bus_in(in), .s(s), .e(e),
    .y(n4x16_decoder_1_out_9));
  RAM_Register_Area_play ram_register_area_play_74 (
    .bus_out(out), .op(out_155), .x(n4x16_decoder_2_out_14), .bus_in(in), .s(s), .e(e),
    .y(n4x16_decoder_1_out_9));
  RAM_Register_Area_play ram_register_area_play_75 (
    .bus_out(out), .op(out_171), .x(n4x16_decoder_2_out_15), .bus_in(in), .s(s), .e(e),
    .y(n4x16_decoder_1_out_9));
  RAM_Register_Area_play ram_register_area_play_76 (
    .bus_out(out), .op(out_187), .x(n4x16_decoder_2_out_16), .bus_in(in), .s(s), .e(e),
    .y(n4x16_decoder_1_out_9));
  RAM_Register_Area_play ram_register_area_play_77 (
    .bus_out(out), .op(out_203), .x(n4x16_decoder_2_out_17), .bus_in(in), .s(s), .e(e),
    .y(n4x16_decoder_1_out_9));
  RAM_Register_Area_play ram_register_area_play_78 (
    .bus_out(out), .op(out_219), .x(n4x16_decoder_2_out_18), .bus_in(in), .s(s), .e(e),
    .y(n4x16_decoder_1_out_9));
  RAM_Register_Area_play ram_register_area_play_79 (
    .bus_out(out), .op(out_235), .x(n4x16_decoder_2_out_19), .bus_in(in), .s(s), .e(e),
    .y(n4x16_decoder_1_out_9));
  RAM_Register_Area_play ram_register_area_play_80 (
    .bus_out(out), .op(out_251), .x(n4x16_decoder_2_out_20), .bus_in(in), .s(s), .e(e),
    .y(n4x16_decoder_1_out_9));
  RAM_Register_Area_play ram_register_area_play_81 (
    .bus_out(out), .op(out_11), .x(n4x16_decoder_2_out_5), .bus_in(in), .s(s), .e(e),
    .y(n4x16_decoder_1_out_10));
  RAM_Register_Area_play ram_register_area_play_82 (
    .bus_out(out), .op(out_28), .x(n4x16_decoder_2_out_6), .bus_in(in), .s(s), .e(e),
    .y(n4x16_decoder_1_out_10));
  RAM_Register_Area_play ram_register_area_play_83 (
    .bus_out(out), .op(out_44), .x(n4x16_decoder_2_out_7), .bus_in(in), .s(s), .e(e),
    .y(n4x16_decoder_1_out_10));
  RAM_Register_Area_play ram_register_area_play_84 (
    .bus_out(out), .op(out_60), .x(n4x16_decoder_2_out_8), .bus_in(in), .s(s), .e(e),
    .y(n4x16_decoder_1_out_10));
  RAM_Register_Area_play ram_register_area_play_85 (
    .bus_out(out), .op(out_76), .x(n4x16_decoder_2_out_9), .bus_in(in), .s(s), .e(e),
    .y(n4x16_decoder_1_out_10));
  RAM_Register_Area_play ram_register_area_play_86 (
    .bus_out(out), .op(out_92), .x(n4x16_decoder_2_out_10), .bus_in(in), .s(s), .e(e),
    .y(n4x16_decoder_1_out_10));
  RAM_Register_Area_play ram_register_area_play_87 (
    .bus_out(out), .op(out_108), .x(n4x16_decoder_2_out_11), .bus_in(in), .s(s), .e(e),
    .y(n4x16_decoder_1_out_10));
  RAM_Register_Area_play ram_register_area_play_88 (
    .bus_out(out), .op(out_124), .x(n4x16_decoder_2_out_12), .bus_in(in), .s(s), .e(e),
    .y(n4x16_decoder_1_out_10));
  RAM_Register_Area_play ram_register_area_play_89 (
    .bus_out(out), .op(out_140), .x(n4x16_decoder_2_out_13), .bus_in(in), .s(s), .e(e),
    .y(n4x16_decoder_1_out_10));
  RAM_Register_Area_play ram_register_area_play_90 (
    .bus_out(out), .op(out_156), .x(n4x16_decoder_2_out_14), .bus_in(in), .s(s), .e(e),
    .y(n4x16_decoder_1_out_10));
  RAM_Register_Area_play ram_register_area_play_91 (
    .bus_out(out), .op(out_172), .x(n4x16_decoder_2_out_15), .bus_in(in), .s(s), .e(e),
    .y(n4x16_decoder_1_out_10));
  RAM_Register_Area_play ram_register_area_play_92 (
    .bus_out(out), .op(out_188), .x(n4x16_decoder_2_out_16), .bus_in(in), .s(s), .e(e),
    .y(n4x16_decoder_1_out_10));
  RAM_Register_Area_play ram_register_area_play_93 (
    .bus_out(out), .op(out_204), .x(n4x16_decoder_2_out_17), .bus_in(in), .s(s), .e(e),
    .y(n4x16_decoder_1_out_10));
  RAM_Register_Area_play ram_register_area_play_94 (
    .bus_out(out), .op(out_220), .x(n4x16_decoder_2_out_18), .bus_in(in), .s(s), .e(e),
    .y(n4x16_decoder_1_out_10));
  RAM_Register_Area_play ram_register_area_play_95 (
    .bus_out(out), .op(out_236), .x(n4x16_decoder_2_out_19), .bus_in(in), .s(s), .e(e),
    .y(n4x16_decoder_1_out_10));
  RAM_Register_Area_play ram_register_area_play_96 (
    .bus_out(out), .op(out_252), .x(n4x16_decoder_2_out_20), .bus_in(in), .s(s), .e(e),
    .y(n4x16_decoder_1_out_10));
  RAM_Register_Area_play ram_register_area_play_97 (
    .bus_out(out), .op(out_12), .x(n4x16_decoder_2_out_5), .bus_in(in), .s(s), .e(e),
    .y(n4x16_decoder_1_out_11));
  RAM_Register_Area_play ram_register_area_play_98 (
    .bus_out(out), .op(out_29), .x(n4x16_decoder_2_out_6), .bus_in(in), .s(s), .e(e),
    .y(n4x16_decoder_1_out_11));
  RAM_Register_Area_play ram_register_area_play_99 (
    .bus_out(out), .op(out_45), .x(n4x16_decoder_2_out_7), .bus_in(in), .s(s), .e(e),
    .y(n4x16_decoder_1_out_11));
  RAM_Register_Area_play ram_register_area_play_100 (
    .bus_out(out), .op(out_61), .x(n4x16_decoder_2_out_8), .bus_in(in), .s(s), .e(e),
    .y(n4x16_decoder_1_out_11));
  RAM_Register_Area_play ram_register_area_play_101 (
    .bus_out(out), .op(out_77), .x(n4x16_decoder_2_out_9), .bus_in(in), .s(s), .e(e),
    .y(n4x16_decoder_1_out_11));
  RAM_Register_Area_play ram_register_area_play_102 (
    .bus_out(out), .op(out_93), .x(n4x16_decoder_2_out_10), .bus_in(in), .s(s), .e(e),
    .y(n4x16_decoder_1_out_11));
  RAM_Register_Area_play ram_register_area_play_103 (
    .bus_out(out), .op(out_109), .x(n4x16_decoder_2_out_11), .bus_in(in), .s(s), .e(e),
    .y(n4x16_decoder_1_out_11));
  RAM_Register_Area_play ram_register_area_play_104 (
    .bus_out(out), .op(out_125), .x(n4x16_decoder_2_out_12), .bus_in(in), .s(s), .e(e),
    .y(n4x16_decoder_1_out_11));
  RAM_Register_Area_play ram_register_area_play_105 (
    .bus_out(out), .op(out_141), .x(n4x16_decoder_2_out_13), .bus_in(in), .s(s), .e(e),
    .y(n4x16_decoder_1_out_11));
  RAM_Register_Area_play ram_register_area_play_106 (
    .bus_out(out), .op(out_157), .x(n4x16_decoder_2_out_14), .bus_in(in), .s(s), .e(e),
    .y(n4x16_decoder_1_out_11));
  RAM_Register_Area_play ram_register_area_play_107 (
    .bus_out(out), .op(out_173), .x(n4x16_decoder_2_out_15), .bus_in(in), .s(s), .e(e),
    .y(n4x16_decoder_1_out_11));
  RAM_Register_Area_play ram_register_area_play_108 (
    .bus_out(out), .op(out_189), .x(n4x16_decoder_2_out_16), .bus_in(in), .s(s), .e(e),
    .y(n4x16_decoder_1_out_11));
  RAM_Register_Area_play ram_register_area_play_109 (
    .bus_out(out), .op(out_205), .x(n4x16_decoder_2_out_17), .bus_in(in), .s(s), .e(e),
    .y(n4x16_decoder_1_out_11));
  RAM_Register_Area_play ram_register_area_play_110 (
    .bus_out(out), .op(out_221), .x(n4x16_decoder_2_out_18), .bus_in(in), .s(s), .e(e),
    .y(n4x16_decoder_1_out_11));
  RAM_Register_Area_play ram_register_area_play_111 (
    .bus_out(out), .op(out_237), .x(n4x16_decoder_2_out_19), .bus_in(in), .s(s), .e(e),
    .y(n4x16_decoder_1_out_11));
  RAM_Register_Area_play ram_register_area_play_112 (
    .bus_out(out), .op(out_253), .x(n4x16_decoder_2_out_20), .bus_in(in), .s(s), .e(e),
    .y(n4x16_decoder_1_out_11));
  RAM_Register_Area_play ram_register_area_play_113 (
    .bus_out(out), .op(out_13), .x(n4x16_decoder_2_out_5), .bus_in(in), .s(s), .e(e),
    .y(n4x16_decoder_1_out_12));
  RAM_Register_Area_play ram_register_area_play_114 (
    .bus_out(out), .op(out_30), .x(n4x16_decoder_2_out_6), .bus_in(in), .s(s), .e(e),
    .y(n4x16_decoder_1_out_12));
  RAM_Register_Area_play ram_register_area_play_115 (
    .bus_out(out), .op(out_46), .x(n4x16_decoder_2_out_7), .bus_in(in), .s(s), .e(e),
    .y(n4x16_decoder_1_out_12));
  RAM_Register_Area_play ram_register_area_play_116 (
    .bus_out(out), .op(out_62), .x(n4x16_decoder_2_out_8), .bus_in(in), .s(s), .e(e),
    .y(n4x16_decoder_1_out_12));
  RAM_Register_Area_play ram_register_area_play_117 (
    .bus_out(out), .op(out_78), .x(n4x16_decoder_2_out_9), .bus_in(in), .s(s), .e(e),
    .y(n4x16_decoder_1_out_12));
  RAM_Register_Area_play ram_register_area_play_118 (
    .bus_out(out), .op(out_94), .x(n4x16_decoder_2_out_10), .bus_in(in), .s(s), .e(e),
    .y(n4x16_decoder_1_out_12));
  RAM_Register_Area_play ram_register_area_play_119 (
    .bus_out(out), .op(out_110), .x(n4x16_decoder_2_out_11), .bus_in(in), .s(s), .e(e),
    .y(n4x16_decoder_1_out_12));
  RAM_Register_Area_play ram_register_area_play_120 (
    .bus_out(out), .op(out_126), .x(n4x16_decoder_2_out_12), .bus_in(in), .s(s), .e(e),
    .y(n4x16_decoder_1_out_12));
  RAM_Register_Area_play ram_register_area_play_121 (
    .bus_out(out), .op(out_142), .x(n4x16_decoder_2_out_13), .bus_in(in), .s(s), .e(e),
    .y(n4x16_decoder_1_out_12));
  RAM_Register_Area_play ram_register_area_play_122 (
    .bus_out(out), .op(out_158), .x(n4x16_decoder_2_out_14), .bus_in(in), .s(s), .e(e),
    .y(n4x16_decoder_1_out_12));
  RAM_Register_Area_play ram_register_area_play_123 (
    .bus_out(out), .op(out_174), .x(n4x16_decoder_2_out_15), .bus_in(in), .s(s), .e(e),
    .y(n4x16_decoder_1_out_12));
  RAM_Register_Area_play ram_register_area_play_124 (
    .bus_out(out), .op(out_190), .x(n4x16_decoder_2_out_16), .bus_in(in), .s(s), .e(e),
    .y(n4x16_decoder_1_out_12));
  RAM_Register_Area_play ram_register_area_play_125 (
    .bus_out(out), .op(out_206), .x(n4x16_decoder_2_out_17), .bus_in(in), .s(s), .e(e),
    .y(n4x16_decoder_1_out_12));
  RAM_Register_Area_play ram_register_area_play_126 (
    .bus_out(out), .op(out_222), .x(n4x16_decoder_2_out_18), .bus_in(in), .s(s), .e(e),
    .y(n4x16_decoder_1_out_12));
  RAM_Register_Area_play ram_register_area_play_127 (
    .bus_out(out), .op(out_238), .x(n4x16_decoder_2_out_19), .bus_in(in), .s(s), .e(e),
    .y(n4x16_decoder_1_out_12));
  RAM_Register_Area_play ram_register_area_play_128 (
    .bus_out(out), .op(out_254), .x(n4x16_decoder_2_out_20), .bus_in(in), .s(s), .e(e),
    .y(n4x16_decoder_1_out_12));
  RAM_Register_Area_play ram_register_area_play_129 (
    .bus_out(out), .op(out_14), .x(n4x16_decoder_2_out_5), .bus_in(in), .s(s), .e(e),
    .y(n4x16_decoder_1_out_13));
  RAM_Register_Area_play ram_register_area_play_130 (
    .bus_out(out), .op(out_31), .x(n4x16_decoder_2_out_6), .bus_in(in), .s(s), .e(e),
    .y(n4x16_decoder_1_out_13));
  RAM_Register_Area_play ram_register_area_play_131 (
    .bus_out(out), .op(out_47), .x(n4x16_decoder_2_out_7), .bus_in(in), .s(s), .e(e),
    .y(n4x16_decoder_1_out_13));
  RAM_Register_Area_play ram_register_area_play_132 (
    .bus_out(out), .op(out_63), .x(n4x16_decoder_2_out_8), .bus_in(in), .s(s), .e(e),
    .y(n4x16_decoder_1_out_13));
  RAM_Register_Area_play ram_register_area_play_133 (
    .bus_out(out), .op(out_79), .x(n4x16_decoder_2_out_9), .bus_in(in), .s(s), .e(e),
    .y(n4x16_decoder_1_out_13));
  RAM_Register_Area_play ram_register_area_play_134 (
    .bus_out(out), .op(out_95), .x(n4x16_decoder_2_out_10), .bus_in(in), .s(s), .e(e),
    .y(n4x16_decoder_1_out_13));
  RAM_Register_Area_play ram_register_area_play_135 (
    .bus_out(out), .op(out_111), .x(n4x16_decoder_2_out_11), .bus_in(in), .s(s), .e(e),
    .y(n4x16_decoder_1_out_13));
  RAM_Register_Area_play ram_register_area_play_136 (
    .bus_out(out), .op(out_127), .x(n4x16_decoder_2_out_12), .bus_in(in), .s(s), .e(e),
    .y(n4x16_decoder_1_out_13));
  RAM_Register_Area_play ram_register_area_play_137 (
    .bus_out(out), .op(out_143), .x(n4x16_decoder_2_out_13), .bus_in(in), .s(s), .e(e),
    .y(n4x16_decoder_1_out_13));
  RAM_Register_Area_play ram_register_area_play_138 (
    .bus_out(out), .op(out_159), .x(n4x16_decoder_2_out_14), .bus_in(in), .s(s), .e(e),
    .y(n4x16_decoder_1_out_13));
  RAM_Register_Area_play ram_register_area_play_139 (
    .bus_out(out), .op(out_175), .x(n4x16_decoder_2_out_15), .bus_in(in), .s(s), .e(e),
    .y(n4x16_decoder_1_out_13));
  RAM_Register_Area_play ram_register_area_play_140 (
    .bus_out(out), .op(out_191), .x(n4x16_decoder_2_out_16), .bus_in(in), .s(s), .e(e),
    .y(n4x16_decoder_1_out_13));
  RAM_Register_Area_play ram_register_area_play_141 (
    .bus_out(out), .op(out_207), .x(n4x16_decoder_2_out_17), .bus_in(in), .s(s), .e(e),
    .y(n4x16_decoder_1_out_13));
  RAM_Register_Area_play ram_register_area_play_142 (
    .bus_out(out), .op(out_223), .x(n4x16_decoder_2_out_18), .bus_in(in), .s(s), .e(e),
    .y(n4x16_decoder_1_out_13));
  RAM_Register_Area_play ram_register_area_play_143 (
    .bus_out(out), .op(out_239), .x(n4x16_decoder_2_out_19), .bus_in(in), .s(s), .e(e),
    .y(n4x16_decoder_1_out_13));
  RAM_Register_Area_play ram_register_area_play_144 (
    .bus_out(out), .op(out_255), .x(n4x16_decoder_2_out_20), .bus_in(in), .s(s), .e(e),
    .y(n4x16_decoder_1_out_13));
  RAM_Register_Area_play ram_register_area_play_145 (
    .bus_out(out), .op(out_15), .x(n4x16_decoder_2_out_5), .bus_in(in), .s(s), .e(e),
    .y(n4x16_decoder_1_out_14));
  RAM_Register_Area_play ram_register_area_play_146 (
    .bus_out(out), .op(out_32), .x(n4x16_decoder_2_out_6), .bus_in(in), .s(s), .e(e),
    .y(n4x16_decoder_1_out_14));
  RAM_Register_Area_play ram_register_area_play_147 (
    .bus_out(out), .op(out_48), .x(n4x16_decoder_2_out_7), .bus_in(in), .s(s), .e(e),
    .y(n4x16_decoder_1_out_14));
  RAM_Register_Area_play ram_register_area_play_148 (
    .bus_out(out), .op(out_64), .x(n4x16_decoder_2_out_8), .bus_in(in), .s(s), .e(e),
    .y(n4x16_decoder_1_out_14));
  RAM_Register_Area_play ram_register_area_play_149 (
    .bus_out(out), .op(out_80), .x(n4x16_decoder_2_out_9), .bus_in(in), .s(s), .e(e),
    .y(n4x16_decoder_1_out_14));
  RAM_Register_Area_play ram_register_area_play_150 (
    .bus_out(out), .op(out_96), .x(n4x16_decoder_2_out_10), .bus_in(in), .s(s), .e(e),
    .y(n4x16_decoder_1_out_14));
  RAM_Register_Area_play ram_register_area_play_151 (
    .bus_out(out), .op(out_112), .x(n4x16_decoder_2_out_11), .bus_in(in), .s(s), .e(e),
    .y(n4x16_decoder_1_out_14));
  RAM_Register_Area_play ram_register_area_play_152 (
    .bus_out(out), .op(out_128), .x(n4x16_decoder_2_out_12), .bus_in(in), .s(s), .e(e),
    .y(n4x16_decoder_1_out_14));
  RAM_Register_Area_play ram_register_area_play_153 (
    .bus_out(out), .op(out_144), .x(n4x16_decoder_2_out_13), .bus_in(in), .s(s), .e(e),
    .y(n4x16_decoder_1_out_14));
  RAM_Register_Area_play ram_register_area_play_154 (
    .bus_out(out), .op(out_160), .x(n4x16_decoder_2_out_14), .bus_in(in), .s(s), .e(e),
    .y(n4x16_decoder_1_out_14));
  RAM_Register_Area_play ram_register_area_play_155 (
    .bus_out(out), .op(out_176), .x(n4x16_decoder_2_out_15), .bus_in(in), .s(s), .e(e),
    .y(n4x16_decoder_1_out_14));
  RAM_Register_Area_play ram_register_area_play_156 (
    .bus_out(out), .op(out_192), .x(n4x16_decoder_2_out_16), .bus_in(in), .s(s), .e(e),
    .y(n4x16_decoder_1_out_14));
  RAM_Register_Area_play ram_register_area_play_157 (
    .bus_out(out), .op(out_208), .x(n4x16_decoder_2_out_17), .bus_in(in), .s(s), .e(e),
    .y(n4x16_decoder_1_out_14));
  RAM_Register_Area_play ram_register_area_play_158 (
    .bus_out(out), .op(out_224), .x(n4x16_decoder_2_out_18), .bus_in(in), .s(s), .e(e),
    .y(n4x16_decoder_1_out_14));
  RAM_Register_Area_play ram_register_area_play_159 (
    .bus_out(out), .op(out_240), .x(n4x16_decoder_2_out_19), .bus_in(in), .s(s), .e(e),
    .y(n4x16_decoder_1_out_14));
  RAM_Register_Area_play ram_register_area_play_160 (
    .bus_out(out), .op(out_256), .x(n4x16_decoder_2_out_20), .bus_in(in), .s(s), .e(e),
    .y(n4x16_decoder_1_out_14));
  RAM_Register_Area_play ram_register_area_play_161 (
    .bus_out(out), .op(out_16), .x(n4x16_decoder_2_out_5), .bus_in(in), .s(s), .e(e),
    .y(n4x16_decoder_1_out_15));
  RAM_Register_Area_play ram_register_area_play_162 (
    .bus_out(out), .op(out_33), .x(n4x16_decoder_2_out_6), .bus_in(in), .s(s), .e(e),
    .y(n4x16_decoder_1_out_15));
  RAM_Register_Area_play ram_register_area_play_163 (
    .bus_out(out), .op(out_49), .x(n4x16_decoder_2_out_7), .bus_in(in), .s(s), .e(e),
    .y(n4x16_decoder_1_out_15));
  RAM_Register_Area_play ram_register_area_play_164 (
    .bus_out(out), .op(out_65), .x(n4x16_decoder_2_out_8), .bus_in(in), .s(s), .e(e),
    .y(n4x16_decoder_1_out_15));
  RAM_Register_Area_play ram_register_area_play_165 (
    .bus_out(out), .op(out_81), .x(n4x16_decoder_2_out_9), .bus_in(in), .s(s), .e(e),
    .y(n4x16_decoder_1_out_15));
  RAM_Register_Area_play ram_register_area_play_166 (
    .bus_out(out), .op(out_97), .x(n4x16_decoder_2_out_10), .bus_in(in), .s(s), .e(e),
    .y(n4x16_decoder_1_out_15));
  RAM_Register_Area_play ram_register_area_play_167 (
    .bus_out(out), .op(out_113), .x(n4x16_decoder_2_out_11), .bus_in(in), .s(s), .e(e),
    .y(n4x16_decoder_1_out_15));
  RAM_Register_Area_play ram_register_area_play_168 (
    .bus_out(out), .op(out_129), .x(n4x16_decoder_2_out_12), .bus_in(in), .s(s), .e(e),
    .y(n4x16_decoder_1_out_15));
  RAM_Register_Area_play ram_register_area_play_169 (
    .bus_out(out), .op(out_145), .x(n4x16_decoder_2_out_13), .bus_in(in), .s(s), .e(e),
    .y(n4x16_decoder_1_out_15));
  RAM_Register_Area_play ram_register_area_play_170 (
    .bus_out(out), .op(out_161), .x(n4x16_decoder_2_out_14), .bus_in(in), .s(s), .e(e),
    .y(n4x16_decoder_1_out_15));
  RAM_Register_Area_play ram_register_area_play_171 (
    .bus_out(out), .op(out_177), .x(n4x16_decoder_2_out_15), .bus_in(in), .s(s), .e(e),
    .y(n4x16_decoder_1_out_15));
  RAM_Register_Area_play ram_register_area_play_172 (
    .bus_out(out), .op(out_193), .x(n4x16_decoder_2_out_16), .bus_in(in), .s(s), .e(e),
    .y(n4x16_decoder_1_out_15));
  RAM_Register_Area_play ram_register_area_play_173 (
    .bus_out(out), .op(out_209), .x(n4x16_decoder_2_out_17), .bus_in(in), .s(s), .e(e),
    .y(n4x16_decoder_1_out_15));
  RAM_Register_Area_play ram_register_area_play_174 (
    .bus_out(out), .op(out_225), .x(n4x16_decoder_2_out_18), .bus_in(in), .s(s), .e(e),
    .y(n4x16_decoder_1_out_15));
  RAM_Register_Area_play ram_register_area_play_175 (
    .bus_out(out), .op(out_241), .x(n4x16_decoder_2_out_19), .bus_in(in), .s(s), .e(e),
    .y(n4x16_decoder_1_out_15));
  RAM_Register_Area_play ram_register_area_play_176 (
    .bus_out(out), .op(out_257), .x(n4x16_decoder_2_out_20), .bus_in(in), .s(s), .e(e),
    .y(n4x16_decoder_1_out_15));
  RAM_Register_Area_play ram_register_area_play_177 (
    .bus_out(out), .op(out_17), .x(n4x16_decoder_2_out_5), .bus_in(in), .s(s), .e(e),
    .y(n4x16_decoder_1_out_16));
  RAM_Register_Area_play ram_register_area_play_178 (
    .bus_out(out), .op(out_34), .x(n4x16_decoder_2_out_6), .bus_in(in), .s(s), .e(e),
    .y(n4x16_decoder_1_out_16));
  RAM_Register_Area_play ram_register_area_play_179 (
    .bus_out(out), .op(out_50), .x(n4x16_decoder_2_out_7), .bus_in(in), .s(s), .e(e),
    .y(n4x16_decoder_1_out_16));
  RAM_Register_Area_play ram_register_area_play_180 (
    .bus_out(out), .op(out_66), .x(n4x16_decoder_2_out_8), .bus_in(in), .s(s), .e(e),
    .y(n4x16_decoder_1_out_16));
  RAM_Register_Area_play ram_register_area_play_181 (
    .bus_out(out), .op(out_82), .x(n4x16_decoder_2_out_9), .bus_in(in), .s(s), .e(e),
    .y(n4x16_decoder_1_out_16));
  RAM_Register_Area_play ram_register_area_play_182 (
    .bus_out(out), .op(out_98), .x(n4x16_decoder_2_out_10), .bus_in(in), .s(s), .e(e),
    .y(n4x16_decoder_1_out_16));
  RAM_Register_Area_play ram_register_area_play_183 (
    .bus_out(out), .op(out_114), .x(n4x16_decoder_2_out_11), .bus_in(in), .s(s), .e(e),
    .y(n4x16_decoder_1_out_16));
  RAM_Register_Area_play ram_register_area_play_184 (
    .bus_out(out), .op(out_130), .x(n4x16_decoder_2_out_12), .bus_in(in), .s(s), .e(e),
    .y(n4x16_decoder_1_out_16));
  RAM_Register_Area_play ram_register_area_play_185 (
    .bus_out(out), .op(out_146), .x(n4x16_decoder_2_out_13), .bus_in(in), .s(s), .e(e),
    .y(n4x16_decoder_1_out_16));
  RAM_Register_Area_play ram_register_area_play_186 (
    .bus_out(out), .op(out_162), .x(n4x16_decoder_2_out_14), .bus_in(in), .s(s), .e(e),
    .y(n4x16_decoder_1_out_16));
  RAM_Register_Area_play ram_register_area_play_187 (
    .bus_out(out), .op(out_178), .x(n4x16_decoder_2_out_15), .bus_in(in), .s(s), .e(e),
    .y(n4x16_decoder_1_out_16));
  RAM_Register_Area_play ram_register_area_play_188 (
    .bus_out(out), .op(out_194), .x(n4x16_decoder_2_out_16), .bus_in(in), .s(s), .e(e),
    .y(n4x16_decoder_1_out_16));
  RAM_Register_Area_play ram_register_area_play_189 (
    .bus_out(out), .op(out_210), .x(n4x16_decoder_2_out_17), .bus_in(in), .s(s), .e(e),
    .y(n4x16_decoder_1_out_16));
  RAM_Register_Area_play ram_register_area_play_190 (
    .bus_out(out), .op(out_226), .x(n4x16_decoder_2_out_18), .bus_in(in), .s(s), .e(e),
    .y(n4x16_decoder_1_out_16));
  RAM_Register_Area_play ram_register_area_play_191 (
    .bus_out(out), .op(out_242), .x(n4x16_decoder_2_out_19), .bus_in(in), .s(s), .e(e),
    .y(n4x16_decoder_1_out_16));
  RAM_Register_Area_play ram_register_area_play_192 (
    .bus_out(out), .op(out_258), .x(n4x16_decoder_2_out_20), .bus_in(in), .s(s), .e(e),
    .y(n4x16_decoder_1_out_16));
  RAM_Register_Area_play ram_register_area_play_193 (
    .bus_out(out), .op(out_18), .x(n4x16_decoder_2_out_5), .bus_in(in), .s(s), .e(e),
    .y(n4x16_decoder_1_out_17));
  RAM_Register_Area_play ram_register_area_play_194 (
    .bus_out(out), .op(out_35), .x(n4x16_decoder_2_out_6), .bus_in(in), .s(s), .e(e),
    .y(n4x16_decoder_1_out_17));
  RAM_Register_Area_play ram_register_area_play_195 (
    .bus_out(out), .op(out_51), .x(n4x16_decoder_2_out_7), .bus_in(in), .s(s), .e(e),
    .y(n4x16_decoder_1_out_17));
  RAM_Register_Area_play ram_register_area_play_196 (
    .bus_out(out), .op(out_67), .x(n4x16_decoder_2_out_8), .bus_in(in), .s(s), .e(e),
    .y(n4x16_decoder_1_out_17));
  RAM_Register_Area_play ram_register_area_play_197 (
    .bus_out(out), .op(out_83), .x(n4x16_decoder_2_out_9), .bus_in(in), .s(s), .e(e),
    .y(n4x16_decoder_1_out_17));
  RAM_Register_Area_play ram_register_area_play_198 (
    .bus_out(out), .op(out_99), .x(n4x16_decoder_2_out_10), .bus_in(in), .s(s), .e(e),
    .y(n4x16_decoder_1_out_17));
  RAM_Register_Area_play ram_register_area_play_199 (
    .bus_out(out), .op(out_115), .x(n4x16_decoder_2_out_11), .bus_in(in), .s(s), .e(e),
    .y(n4x16_decoder_1_out_17));
  RAM_Register_Area_play ram_register_area_play_200 (
    .bus_out(out), .op(out_131), .x(n4x16_decoder_2_out_12), .bus_in(in), .s(s), .e(e),
    .y(n4x16_decoder_1_out_17));
  RAM_Register_Area_play ram_register_area_play_201 (
    .bus_out(out), .op(out_147), .x(n4x16_decoder_2_out_13), .bus_in(in), .s(s), .e(e),
    .y(n4x16_decoder_1_out_17));
  RAM_Register_Area_play ram_register_area_play_202 (
    .bus_out(out), .op(out_163), .x(n4x16_decoder_2_out_14), .bus_in(in), .s(s), .e(e),
    .y(n4x16_decoder_1_out_17));
  RAM_Register_Area_play ram_register_area_play_203 (
    .bus_out(out), .op(out_179), .x(n4x16_decoder_2_out_15), .bus_in(in), .s(s), .e(e),
    .y(n4x16_decoder_1_out_17));
  RAM_Register_Area_play ram_register_area_play_204 (
    .bus_out(out), .op(out_195), .x(n4x16_decoder_2_out_16), .bus_in(in), .s(s), .e(e),
    .y(n4x16_decoder_1_out_17));
  RAM_Register_Area_play ram_register_area_play_205 (
    .bus_out(out), .op(out_211), .x(n4x16_decoder_2_out_17), .bus_in(in), .s(s), .e(e),
    .y(n4x16_decoder_1_out_17));
  RAM_Register_Area_play ram_register_area_play_206 (
    .bus_out(out), .op(out_227), .x(n4x16_decoder_2_out_18), .bus_in(in), .s(s), .e(e),
    .y(n4x16_decoder_1_out_17));
  RAM_Register_Area_play ram_register_area_play_207 (
    .bus_out(out), .op(out_243), .x(n4x16_decoder_2_out_19), .bus_in(in), .s(s), .e(e),
    .y(n4x16_decoder_1_out_17));
  RAM_Register_Area_play ram_register_area_play_208 (
    .bus_out(out), .op(out_259), .x(n4x16_decoder_2_out_20), .bus_in(in), .s(s), .e(e),
    .y(n4x16_decoder_1_out_17));
  RAM_Register_Area_play ram_register_area_play_209 (
    .bus_out(out), .op(out_19), .x(n4x16_decoder_2_out_5), .bus_in(in), .s(s), .e(e),
    .y(n4x16_decoder_1_out_18));
  RAM_Register_Area_play ram_register_area_play_210 (
    .bus_out(out), .op(out_36), .x(n4x16_decoder_2_out_6), .bus_in(in), .s(s), .e(e),
    .y(n4x16_decoder_1_out_18));
  RAM_Register_Area_play ram_register_area_play_211 (
    .bus_out(out), .op(out_52), .x(n4x16_decoder_2_out_7), .bus_in(in), .s(s), .e(e),
    .y(n4x16_decoder_1_out_18));
  RAM_Register_Area_play ram_register_area_play_212 (
    .bus_out(out), .op(out_68), .x(n4x16_decoder_2_out_8), .bus_in(in), .s(s), .e(e),
    .y(n4x16_decoder_1_out_18));
  RAM_Register_Area_play ram_register_area_play_213 (
    .bus_out(out), .op(out_84), .x(n4x16_decoder_2_out_9), .bus_in(in), .s(s), .e(e),
    .y(n4x16_decoder_1_out_18));
  RAM_Register_Area_play ram_register_area_play_214 (
    .bus_out(out), .op(out_100), .x(n4x16_decoder_2_out_10), .bus_in(in), .s(s), .e(e),
    .y(n4x16_decoder_1_out_18));
  RAM_Register_Area_play ram_register_area_play_215 (
    .bus_out(out), .op(out_116), .x(n4x16_decoder_2_out_11), .bus_in(in), .s(s), .e(e),
    .y(n4x16_decoder_1_out_18));
  RAM_Register_Area_play ram_register_area_play_216 (
    .bus_out(out), .op(out_132), .x(n4x16_decoder_2_out_12), .bus_in(in), .s(s), .e(e),
    .y(n4x16_decoder_1_out_18));
  RAM_Register_Area_play ram_register_area_play_217 (
    .bus_out(out), .op(out_148), .x(n4x16_decoder_2_out_13), .bus_in(in), .s(s), .e(e),
    .y(n4x16_decoder_1_out_18));
  RAM_Register_Area_play ram_register_area_play_218 (
    .bus_out(out), .op(out_164), .x(n4x16_decoder_2_out_14), .bus_in(in), .s(s), .e(e),
    .y(n4x16_decoder_1_out_18));
  RAM_Register_Area_play ram_register_area_play_219 (
    .bus_out(out), .op(out_180), .x(n4x16_decoder_2_out_15), .bus_in(in), .s(s), .e(e),
    .y(n4x16_decoder_1_out_18));
  RAM_Register_Area_play ram_register_area_play_220 (
    .bus_out(out), .op(out_196), .x(n4x16_decoder_2_out_16), .bus_in(in), .s(s), .e(e),
    .y(n4x16_decoder_1_out_18));
  RAM_Register_Area_play ram_register_area_play_221 (
    .bus_out(out), .op(out_212), .x(n4x16_decoder_2_out_17), .bus_in(in), .s(s), .e(e),
    .y(n4x16_decoder_1_out_18));
  RAM_Register_Area_play ram_register_area_play_222 (
    .bus_out(out), .op(out_228), .x(n4x16_decoder_2_out_18), .bus_in(in), .s(s), .e(e),
    .y(n4x16_decoder_1_out_18));
  RAM_Register_Area_play ram_register_area_play_223 (
    .bus_out(out), .op(out_244), .x(n4x16_decoder_2_out_19), .bus_in(in), .s(s), .e(e),
    .y(n4x16_decoder_1_out_18));
  RAM_Register_Area_play ram_register_area_play_224 (
    .bus_out(out), .op(out_260), .x(n4x16_decoder_2_out_20), .bus_in(in), .s(s), .e(e),
    .y(n4x16_decoder_1_out_18));
  RAM_Register_Area_play ram_register_area_play_225 (
    .bus_out(out), .op(out_20), .x(n4x16_decoder_2_out_5), .bus_in(in), .s(s), .e(e),
    .y(n4x16_decoder_1_out_19));
  RAM_Register_Area_play ram_register_area_play_226 (
    .bus_out(out), .op(out_37), .x(n4x16_decoder_2_out_6), .bus_in(in), .s(s), .e(e),
    .y(n4x16_decoder_1_out_19));
  RAM_Register_Area_play ram_register_area_play_227 (
    .bus_out(out), .op(out_53), .x(n4x16_decoder_2_out_7), .bus_in(in), .s(s), .e(e),
    .y(n4x16_decoder_1_out_19));
  RAM_Register_Area_play ram_register_area_play_228 (
    .bus_out(out), .op(out_69), .x(n4x16_decoder_2_out_8), .bus_in(in), .s(s), .e(e),
    .y(n4x16_decoder_1_out_19));
  RAM_Register_Area_play ram_register_area_play_229 (
    .bus_out(out), .op(out_85), .x(n4x16_decoder_2_out_9), .bus_in(in), .s(s), .e(e),
    .y(n4x16_decoder_1_out_19));
  RAM_Register_Area_play ram_register_area_play_230 (
    .bus_out(out), .op(out_101), .x(n4x16_decoder_2_out_10), .bus_in(in), .s(s), .e(e),
    .y(n4x16_decoder_1_out_19));
  RAM_Register_Area_play ram_register_area_play_231 (
    .bus_out(out), .op(out_117), .x(n4x16_decoder_2_out_11), .bus_in(in), .s(s), .e(e),
    .y(n4x16_decoder_1_out_19));
  RAM_Register_Area_play ram_register_area_play_232 (
    .bus_out(out), .op(out_133), .x(n4x16_decoder_2_out_12), .bus_in(in), .s(s), .e(e),
    .y(n4x16_decoder_1_out_19));
  RAM_Register_Area_play ram_register_area_play_233 (
    .bus_out(out), .op(out_149), .x(n4x16_decoder_2_out_13), .bus_in(in), .s(s), .e(e),
    .y(n4x16_decoder_1_out_19));
  RAM_Register_Area_play ram_register_area_play_234 (
    .bus_out(out), .op(out_165), .x(n4x16_decoder_2_out_14), .bus_in(in), .s(s), .e(e),
    .y(n4x16_decoder_1_out_19));
  RAM_Register_Area_play ram_register_area_play_235 (
    .bus_out(out), .op(out_181), .x(n4x16_decoder_2_out_15), .bus_in(in), .s(s), .e(e),
    .y(n4x16_decoder_1_out_19));
  RAM_Register_Area_play ram_register_area_play_236 (
    .bus_out(out), .op(out_197), .x(n4x16_decoder_2_out_16), .bus_in(in), .s(s), .e(e),
    .y(n4x16_decoder_1_out_19));
  RAM_Register_Area_play ram_register_area_play_237 (
    .bus_out(out), .op(out_213), .x(n4x16_decoder_2_out_17), .bus_in(in), .s(s), .e(e),
    .y(n4x16_decoder_1_out_19));
  RAM_Register_Area_play ram_register_area_play_238 (
    .bus_out(out), .op(out_229), .x(n4x16_decoder_2_out_18), .bus_in(in), .s(s), .e(e),
    .y(n4x16_decoder_1_out_19));
  RAM_Register_Area_play ram_register_area_play_239 (
    .bus_out(out), .op(out_245), .x(n4x16_decoder_2_out_19), .bus_in(in), .s(s), .e(e),
    .y(n4x16_decoder_1_out_19));
  RAM_Register_Area_play ram_register_area_play_240 (
    .bus_out(out), .op(out_261), .x(n4x16_decoder_2_out_20), .bus_in(in), .s(s), .e(e),
    .y(n4x16_decoder_1_out_19));
  RAM_Register_Area_play ram_register_area_play_241 (
    .bus_out(out), .op(out_21), .x(n4x16_decoder_2_out_5), .bus_in(in), .s(s), .e(e),
    .y(n4x16_decoder_1_out_20));
  RAM_Register_Area_play ram_register_area_play_242 (
    .bus_out(out), .op(out_38), .x(n4x16_decoder_2_out_6), .bus_in(in), .s(s), .e(e),
    .y(n4x16_decoder_1_out_20));
  RAM_Register_Area_play ram_register_area_play_243 (
    .bus_out(out), .op(out_54), .x(n4x16_decoder_2_out_7), .bus_in(in), .s(s), .e(e),
    .y(n4x16_decoder_1_out_20));
  RAM_Register_Area_play ram_register_area_play_244 (
    .bus_out(out), .op(out_70), .x(n4x16_decoder_2_out_8), .bus_in(in), .s(s), .e(e),
    .y(n4x16_decoder_1_out_20));
  RAM_Register_Area_play ram_register_area_play_245 (
    .bus_out(out), .op(out_86), .x(n4x16_decoder_2_out_9), .bus_in(in), .s(s), .e(e),
    .y(n4x16_decoder_1_out_20));
  RAM_Register_Area_play ram_register_area_play_246 (
    .bus_out(out), .op(out_102), .x(n4x16_decoder_2_out_10), .bus_in(in), .s(s), .e(e),
    .y(n4x16_decoder_1_out_20));
  RAM_Register_Area_play ram_register_area_play_247 (
    .bus_out(out), .op(out_118), .x(n4x16_decoder_2_out_11), .bus_in(in), .s(s), .e(e),
    .y(n4x16_decoder_1_out_20));
  RAM_Register_Area_play ram_register_area_play_248 (
    .bus_out(out), .op(out_134), .x(n4x16_decoder_2_out_12), .bus_in(in), .s(s), .e(e),
    .y(n4x16_decoder_1_out_20));
  RAM_Register_Area_play ram_register_area_play_249 (
    .bus_out(out), .op(out_150), .x(n4x16_decoder_2_out_13), .bus_in(in), .s(s), .e(e),
    .y(n4x16_decoder_1_out_20));
  RAM_Register_Area_play ram_register_area_play_250 (
    .bus_out(out), .op(out_166), .x(n4x16_decoder_2_out_14), .bus_in(in), .s(s), .e(e),
    .y(n4x16_decoder_1_out_20));
  RAM_Register_Area_play ram_register_area_play_251 (
    .bus_out(out), .op(out_182), .x(n4x16_decoder_2_out_15), .bus_in(in), .s(s), .e(e),
    .y(n4x16_decoder_1_out_20));
  RAM_Register_Area_play ram_register_area_play_252 (
    .bus_out(out), .op(out_198), .x(n4x16_decoder_2_out_16), .bus_in(in), .s(s), .e(e),
    .y(n4x16_decoder_1_out_20));
  RAM_Register_Area_play ram_register_area_play_253 (
    .bus_out(out), .op(out_214), .x(n4x16_decoder_2_out_17), .bus_in(in), .s(s), .e(e),
    .y(n4x16_decoder_1_out_20));
  RAM_Register_Area_play ram_register_area_play_254 (
    .bus_out(out), .op(out_230), .x(n4x16_decoder_2_out_18), .bus_in(in), .s(s), .e(e),
    .y(n4x16_decoder_1_out_20));
  RAM_Register_Area_play ram_register_area_play_255 (
    .bus_out(out), .op(out_246), .x(n4x16_decoder_2_out_19), .bus_in(in), .s(s), .e(e),
    .y(n4x16_decoder_1_out_20));
  RAM_Register_Area_play ram_register_area_play_256 (
    .bus_out(out), .op(out_262), .x(n4x16_decoder_2_out_20), .bus_in(in), .s(s), .e(e),
    .y(n4x16_decoder_1_out_20));
endmodule

module MAR (
  input  [7:0] i,
  input  sa,
  output out_3,
  output out_4,
  output out_5,
  output out_6,
  output out_7,
  output out_8,
  output out_9,
  output out_10
);

  _8_bit_Memory u_8_bit_memory_1 (
    .o(out_3), .o_2(out_4), .o_3(out_5), .o_4(out_6), .o_5(out_7), .o_6(out_8), .o_7(out_9), .o_8(out_10),
    .i_2(i[1]), .i_3(i[2]), .i_4(i[3]), .i_5(i[4]), .i_6(i[5]), .i_7(i[6]), .i_8(i[7]), .s(sa), .i(i[0]));
endmodule

module RAM_Register (
  input  [7:0] i,
  input  s,
  input  e,
  output [7:0] out_4
);

  wire [7:0] n1_byte_enabler_1_o, n1_byte_memory_1_o;

  _1_byte_Memory u_1_byte_memory_1 (.o(n1_byte_memory_1_o), .i(i), .s(s));
  _1_byte_Enabler u_1_byte_enabler_1 (.o(n1_byte_enabler_1_o), .i(n1_byte_memory_1_o), .e(e));
  assign out_4 = e ? n1_byte_enabler_1_o : 8'bz;  // Controlled_Buffer controlled_buffer_1
endmodule

module RAM_Register_Area (
  input  y,
  input  x,
  input  [7:0] bus_in,
  input  s,
  input  e,
  output [7:0] bus_out
);

  wire and_1_out, and_2_out, X_out;
  wire [7:0] ram_register_1_out_4, undriven;

  and u_X (X_out, x, y);
  and and_1 (and_1_out, X_out, s);
  and and_2 (and_2_out, X_out, e);
  assign bus_in = X_out ? undriven : 8'bz;  // Controlled_Buffer controlled_buffer_1
  RAM_Register ram_register_1 (.out_4(ram_register_1_out_4), .i(undriven), .s(and_1_out), .e(and_2_out));
  assign bus_out = X_out ? ram_register_1_out_4 : 8'bz;  // Controlled_Buffer controlled_buffer_2
endmodule

module RAM_256 (
  input  [7:0] Address,
  input  sa,
  input  s,
  input  e,
  input  [7:0] in,
  output [7:0] out
);

  wire mar_1_out_3, mar_1_out_4, mar_1_out_5, mar_1_out_6, mar_1_out_7, mar_1_out_8, mar_1_out_9,
       mar_1_out_10, n4x16_decoder_1_out_5, n4x16_decoder_1_out_6, n4x16_decoder_1_out_7,
       n4x16_decoder_1_out_8, n4x16_decoder_1_out_9, n4x16_decoder_1_out_10, n4x16_decoder_1_out_11,
       n4x16_decoder_1_out_12, n4x16_decoder_1_out_13, n4x16_decoder_1_out_14, n4x16_decoder_1_out_15,
       n4x16_decoder_1_out_16, n4x16_decoder_1_out_17, n4x16_decoder_1_out_18, n4x16_decoder_1_out_19,
       n4x16_decoder_1_out_20, n4x16_decoder_2_out_5, n4x16_decoder_2_out_6, n4x16_decoder_2_out_7,
       n4x16_decoder_2_out_8, n4x16_decoder_2_out_9, n4x16_decoder_2_out_10, n4x16_decoder_2_out_11,
       n4x16_decoder_2_out_12, n4x16_decoder_2_out_13, n4x16_decoder_2_out_14, n4x16_decoder_2_out_15,
       n4x16_decoder_2_out_16, n4x16_decoder_2_out_17, n4x16_decoder_2_out_18, n4x16_decoder_2_out_19,
       n4x16_decoder_2_out_20;

  _4x16_Decoder u_4x16_decoder_1 (
    .out_20(n4x16_decoder_1_out_20), .out_5(n4x16_decoder_1_out_5), .out_6(n4x16_decoder_1_out_6),
    .out_7(n4x16_decoder_1_out_7), .out_8(n4x16_decoder_1_out_8), .out_9(n4x16_decoder_1_out_9),
    .out_10(n4x16_decoder_1_out_10), .out_11(n4x16_decoder_1_out_11), .out_12(n4x16_decoder_1_out_12),
    .out_13(n4x16_decoder_1_out_13), .out_14(n4x16_decoder_1_out_14), .out_15(n4x16_decoder_1_out_15),
    .out_16(n4x16_decoder_1_out_16), .out_17(n4x16_decoder_1_out_17), .out_18(n4x16_decoder_1_out_18),
    .out_19(n4x16_decoder_1_out_19), .d(mar_1_out_3), .a(mar_1_out_6), .b(mar_1_out_5), .c(mar_1_out_4));
  MAR mar_1 (
    .out_3(mar_1_out_3), .out_4(mar_1_out_4), .out_5(mar_1_out_5), .out_6(mar_1_out_6), .out_7(mar_1_out_7),
    .out_8(mar_1_out_8), .out_9(mar_1_out_9), .out_10(mar_1_out_10), .i(Address), .sa(sa));
  _4x16_Decoder u_4x16_decoder_2 (
    .out_20(n4x16_decoder_2_out_20), .out_5(n4x16_decoder_2_out_5), .out_6(n4x16_decoder_2_out_6),
    .out_7(n4x16_decoder_2_out_7), .out_8(n4x16_decoder_2_out_8), .out_9(n4x16_decoder_2_out_9),
    .out_10(n4x16_decoder_2_out_10), .out_11(n4x16_decoder_2_out_11), .out_12(n4x16_decoder_2_out_12),
    .out_13(n4x16_decoder_2_out_13), .out_14(n4x16_decoder_2_out_14), .out_15(n4x16_decoder_2_out_15),
    .out_16(n4x16_decoder_2_out_16), .out_17(n4x16_decoder_2_out_17), .out_18(n4x16_decoder_2_out_18),
    .out_19(n4x16_decoder_2_out_19), .d(mar_1_out_7), .a(mar_1_out_10), .b(mar_1_out_9), .c(mar_1_out_8));
  RAM_Register_Area ram_register_area_1 (
    .bus_out(out), .x(n4x16_decoder_2_out_5), .bus_in(in), .s(s), .e(e), .y(n4x16_decoder_1_out_5));
  RAM_Register_Area ram_register_area_2 (
    .bus_out(out), .x(n4x16_decoder_2_out_6), .bus_in(in), .s(s), .e(e), .y(n4x16_decoder_1_out_5));
  RAM_Register_Area ram_register_area_3 (
    .bus_out(out), .x(n4x16_decoder_2_out_7), .bus_in(in), .s(s), .e(e), .y(n4x16_decoder_1_out_5));
  RAM_Register_Area ram_register_area_4 (
    .bus_out(out), .x(n4x16_decoder_2_out_8), .bus_in(in), .s(s), .e(e), .y(n4x16_decoder_1_out_5));
  RAM_Register_Area ram_register_area_5 (
    .bus_out(out), .x(n4x16_decoder_2_out_9), .bus_in(in), .s(s), .e(e), .y(n4x16_decoder_1_out_5));
  RAM_Register_Area ram_register_area_6 (
    .bus_out(out), .x(n4x16_decoder_2_out_10), .bus_in(in), .s(s), .e(e), .y(n4x16_decoder_1_out_5));
  RAM_Register_Area ram_register_area_7 (
    .bus_out(out), .x(n4x16_decoder_2_out_11), .bus_in(in), .s(s), .e(e), .y(n4x16_decoder_1_out_5));
  RAM_Register_Area ram_register_area_8 (
    .bus_out(out), .x(n4x16_decoder_2_out_12), .bus_in(in), .s(s), .e(e), .y(n4x16_decoder_1_out_5));
  RAM_Register_Area ram_register_area_9 (
    .bus_out(out), .x(n4x16_decoder_2_out_13), .bus_in(in), .s(s), .e(e), .y(n4x16_decoder_1_out_5));
  RAM_Register_Area ram_register_area_10 (
    .bus_out(out), .x(n4x16_decoder_2_out_14), .bus_in(in), .s(s), .e(e), .y(n4x16_decoder_1_out_5));
  RAM_Register_Area ram_register_area_11 (
    .bus_out(out), .x(n4x16_decoder_2_out_15), .bus_in(in), .s(s), .e(e), .y(n4x16_decoder_1_out_5));
  RAM_Register_Area ram_register_area_12 (
    .bus_out(out), .x(n4x16_decoder_2_out_16), .bus_in(in), .s(s), .e(e), .y(n4x16_decoder_1_out_5));
  RAM_Register_Area ram_register_area_13 (
    .bus_out(out), .x(n4x16_decoder_2_out_17), .bus_in(in), .s(s), .e(e), .y(n4x16_decoder_1_out_5));
  RAM_Register_Area ram_register_area_14 (
    .bus_out(out), .x(n4x16_decoder_2_out_18), .bus_in(in), .s(s), .e(e), .y(n4x16_decoder_1_out_5));
  RAM_Register_Area ram_register_area_15 (
    .bus_out(out), .x(n4x16_decoder_2_out_19), .bus_in(in), .s(s), .e(e), .y(n4x16_decoder_1_out_5));
  RAM_Register_Area ram_register_area_16 (
    .bus_out(out), .x(n4x16_decoder_2_out_20), .bus_in(in), .s(s), .e(e), .y(n4x16_decoder_1_out_5));
  RAM_Register_Area ram_register_area_17 (
    .bus_out(out), .x(n4x16_decoder_2_out_5), .bus_in(in), .s(s), .e(e), .y(n4x16_decoder_1_out_6));
  RAM_Register_Area ram_register_area_18 (
    .bus_out(out), .x(n4x16_decoder_2_out_6), .bus_in(in), .s(s), .e(e), .y(n4x16_decoder_1_out_6));
  RAM_Register_Area ram_register_area_19 (
    .bus_out(out), .x(n4x16_decoder_2_out_7), .bus_in(in), .s(s), .e(e), .y(n4x16_decoder_1_out_6));
  RAM_Register_Area ram_register_area_20 (
    .bus_out(out), .x(n4x16_decoder_2_out_8), .bus_in(in), .s(s), .e(e), .y(n4x16_decoder_1_out_6));
  RAM_Register_Area ram_register_area_21 (
    .bus_out(out), .x(n4x16_decoder_2_out_9), .bus_in(in), .s(s), .e(e), .y(n4x16_decoder_1_out_6));
  RAM_Register_Area ram_register_area_22 (
    .bus_out(out), .x(n4x16_decoder_2_out_10), .bus_in(in), .s(s), .e(e), .y(n4x16_decoder_1_out_6));
  RAM_Register_Area ram_register_area_23 (
    .bus_out(out), .x(n4x16_decoder_2_out_11), .bus_in(in), .s(s), .e(e), .y(n4x16_decoder_1_out_6));
  RAM_Register_Area ram_register_area_24 (
    .bus_out(out), .x(n4x16_decoder_2_out_12), .bus_in(in), .s(s), .e(e), .y(n4x16_decoder_1_out_6));
  RAM_Register_Area ram_register_area_25 (
    .bus_out(out), .x(n4x16_decoder_2_out_13), .bus_in(in), .s(s), .e(e), .y(n4x16_decoder_1_out_6));
  RAM_Register_Area ram_register_area_26 (
    .bus_out(out), .x(n4x16_decoder_2_out_14), .bus_in(in), .s(s), .e(e), .y(n4x16_decoder_1_out_6));
  RAM_Register_Area ram_register_area_27 (
    .bus_out(out), .x(n4x16_decoder_2_out_15), .bus_in(in), .s(s), .e(e), .y(n4x16_decoder_1_out_6));
  RAM_Register_Area ram_register_area_28 (
    .bus_out(out), .x(n4x16_decoder_2_out_16), .bus_in(in), .s(s), .e(e), .y(n4x16_decoder_1_out_6));
  RAM_Register_Area ram_register_area_29 (
    .bus_out(out), .x(n4x16_decoder_2_out_17), .bus_in(in), .s(s), .e(e), .y(n4x16_decoder_1_out_6));
  RAM_Register_Area ram_register_area_30 (
    .bus_out(out), .x(n4x16_decoder_2_out_18), .bus_in(in), .s(s), .e(e), .y(n4x16_decoder_1_out_6));
  RAM_Register_Area ram_register_area_31 (
    .bus_out(out), .x(n4x16_decoder_2_out_19), .bus_in(in), .s(s), .e(e), .y(n4x16_decoder_1_out_6));
  RAM_Register_Area ram_register_area_32 (
    .bus_out(out), .x(n4x16_decoder_2_out_20), .bus_in(in), .s(s), .e(e), .y(n4x16_decoder_1_out_6));
  RAM_Register_Area ram_register_area_33 (
    .bus_out(out), .x(n4x16_decoder_2_out_5), .bus_in(in), .s(s), .e(e), .y(n4x16_decoder_1_out_7));
  RAM_Register_Area ram_register_area_34 (
    .bus_out(out), .x(n4x16_decoder_2_out_6), .bus_in(in), .s(s), .e(e), .y(n4x16_decoder_1_out_7));
  RAM_Register_Area ram_register_area_35 (
    .bus_out(out), .x(n4x16_decoder_2_out_7), .bus_in(in), .s(s), .e(e), .y(n4x16_decoder_1_out_7));
  RAM_Register_Area ram_register_area_36 (
    .bus_out(out), .x(n4x16_decoder_2_out_8), .bus_in(in), .s(s), .e(e), .y(n4x16_decoder_1_out_7));
  RAM_Register_Area ram_register_area_37 (
    .bus_out(out), .x(n4x16_decoder_2_out_9), .bus_in(in), .s(s), .e(e), .y(n4x16_decoder_1_out_7));
  RAM_Register_Area ram_register_area_38 (
    .bus_out(out), .x(n4x16_decoder_2_out_10), .bus_in(in), .s(s), .e(e), .y(n4x16_decoder_1_out_7));
  RAM_Register_Area ram_register_area_39 (
    .bus_out(out), .x(n4x16_decoder_2_out_11), .bus_in(in), .s(s), .e(e), .y(n4x16_decoder_1_out_7));
  RAM_Register_Area ram_register_area_40 (
    .bus_out(out), .x(n4x16_decoder_2_out_12), .bus_in(in), .s(s), .e(e), .y(n4x16_decoder_1_out_7));
  RAM_Register_Area ram_register_area_41 (
    .bus_out(out), .x(n4x16_decoder_2_out_13), .bus_in(in), .s(s), .e(e), .y(n4x16_decoder_1_out_7));
  RAM_Register_Area ram_register_area_42 (
    .bus_out(out), .x(n4x16_decoder_2_out_14), .bus_in(in), .s(s), .e(e), .y(n4x16_decoder_1_out_7));
  RAM_Register_Area ram_register_area_43 (
    .bus_out(out), .x(n4x16_decoder_2_out_15), .bus_in(in), .s(s), .e(e), .y(n4x16_decoder_1_out_7));
  RAM_Register_Area ram_register_area_44 (
    .bus_out(out), .x(n4x16_decoder_2_out_16), .bus_in(in), .s(s), .e(e), .y(n4x16_decoder_1_out_7));
  RAM_Register_Area ram_register_area_45 (
    .bus_out(out), .x(n4x16_decoder_2_out_17), .bus_in(in), .s(s), .e(e), .y(n4x16_decoder_1_out_7));
  RAM_Register_Area ram_register_area_46 (
    .bus_out(out), .x(n4x16_decoder_2_out_18), .bus_in(in), .s(s), .e(e), .y(n4x16_decoder_1_out_7));
  RAM_Register_Area ram_register_area_47 (
    .bus_out(out), .x(n4x16_decoder_2_out_19), .bus_in(in), .s(s), .e(e), .y(n4x16_decoder_1_out_7));
  RAM_Register_Area ram_register_area_48 (
    .bus_out(out), .x(n4x16_decoder_2_out_20), .bus_in(in), .s(s), .e(e), .y(n4x16_decoder_1_out_7));
  RAM_Register_Area ram_register_area_49 (
    .bus_out(out), .x(n4x16_decoder_2_out_5), .bus_in(in), .s(s), .e(e), .y(n4x16_decoder_1_out_8));
  RAM_Register_Area ram_register_area_50 (
    .bus_out(out), .x(n4x16_decoder_2_out_6), .bus_in(in), .s(s), .e(e), .y(n4x16_decoder_1_out_8));
  RAM_Register_Area ram_register_area_51 (
    .bus_out(out), .x(n4x16_decoder_2_out_7), .bus_in(in), .s(s), .e(e), .y(n4x16_decoder_1_out_8));
  RAM_Register_Area ram_register_area_52 (
    .bus_out(out), .x(n4x16_decoder_2_out_8), .bus_in(in), .s(s), .e(e), .y(n4x16_decoder_1_out_8));
  RAM_Register_Area ram_register_area_53 (
    .bus_out(out), .x(n4x16_decoder_2_out_9), .bus_in(in), .s(s), .e(e), .y(n4x16_decoder_1_out_8));
  RAM_Register_Area ram_register_area_54 (
    .bus_out(out), .x(n4x16_decoder_2_out_10), .bus_in(in), .s(s), .e(e), .y(n4x16_decoder_1_out_8));
  RAM_Register_Area ram_register_area_55 (
    .bus_out(out), .x(n4x16_decoder_2_out_11), .bus_in(in), .s(s), .e(e), .y(n4x16_decoder_1_out_8));
  RAM_Register_Area ram_register_area_56 (
    .bus_out(out), .x(n4x16_decoder_2_out_12), .bus_in(in), .s(s), .e(e), .y(n4x16_decoder_1_out_8));
  RAM_Register_Area ram_register_area_57 (
    .bus_out(out), .x(n4x16_decoder_2_out_13), .bus_in(in), .s(s), .e(e), .y(n4x16_decoder_1_out_8));
  RAM_Register_Area ram_register_area_58 (
    .bus_out(out), .x(n4x16_decoder_2_out_14), .bus_in(in), .s(s), .e(e), .y(n4x16_decoder_1_out_8));
  RAM_Register_Area ram_register_area_59 (
    .bus_out(out), .x(n4x16_decoder_2_out_15), .bus_in(in), .s(s), .e(e), .y(n4x16_decoder_1_out_8));
  RAM_Register_Area ram_register_area_60 (
    .bus_out(out), .x(n4x16_decoder_2_out_16), .bus_in(in), .s(s), .e(e), .y(n4x16_decoder_1_out_8));
  RAM_Register_Area ram_register_area_61 (
    .bus_out(out), .x(n4x16_decoder_2_out_17), .bus_in(in), .s(s), .e(e), .y(n4x16_decoder_1_out_8));
  RAM_Register_Area ram_register_area_62 (
    .bus_out(out), .x(n4x16_decoder_2_out_18), .bus_in(in), .s(s), .e(e), .y(n4x16_decoder_1_out_8));
  RAM_Register_Area ram_register_area_63 (
    .bus_out(out), .x(n4x16_decoder_2_out_19), .bus_in(in), .s(s), .e(e), .y(n4x16_decoder_1_out_8));
  RAM_Register_Area ram_register_area_64 (
    .bus_out(out), .x(n4x16_decoder_2_out_20), .bus_in(in), .s(s), .e(e), .y(n4x16_decoder_1_out_8));
  RAM_Register_Area ram_register_area_65 (
    .bus_out(out), .x(n4x16_decoder_2_out_5), .bus_in(in), .s(s), .e(e), .y(n4x16_decoder_1_out_9));
  RAM_Register_Area ram_register_area_66 (
    .bus_out(out), .x(n4x16_decoder_2_out_6), .bus_in(in), .s(s), .e(e), .y(n4x16_decoder_1_out_9));
  RAM_Register_Area ram_register_area_67 (
    .bus_out(out), .x(n4x16_decoder_2_out_7), .bus_in(in), .s(s), .e(e), .y(n4x16_decoder_1_out_9));
  RAM_Register_Area ram_register_area_68 (
    .bus_out(out), .x(n4x16_decoder_2_out_8), .bus_in(in), .s(s), .e(e), .y(n4x16_decoder_1_out_9));
  RAM_Register_Area ram_register_area_69 (
    .bus_out(out), .x(n4x16_decoder_2_out_9), .bus_in(in), .s(s), .e(e), .y(n4x16_decoder_1_out_9));
  RAM_Register_Area ram_register_area_70 (
    .bus_out(out), .x(n4x16_decoder_2_out_10), .bus_in(in), .s(s), .e(e), .y(n4x16_decoder_1_out_9));
  RAM_Register_Area ram_register_area_71 (
    .bus_out(out), .x(n4x16_decoder_2_out_11), .bus_in(in), .s(s), .e(e), .y(n4x16_decoder_1_out_9));
  RAM_Register_Area ram_register_area_72 (
    .bus_out(out), .x(n4x16_decoder_2_out_12), .bus_in(in), .s(s), .e(e), .y(n4x16_decoder_1_out_9));
  RAM_Register_Area ram_register_area_73 (
    .bus_out(out), .x(n4x16_decoder_2_out_13), .bus_in(in), .s(s), .e(e), .y(n4x16_decoder_1_out_9));
  RAM_Register_Area ram_register_area_74 (
    .bus_out(out), .x(n4x16_decoder_2_out_14), .bus_in(in), .s(s), .e(e), .y(n4x16_decoder_1_out_9));
  RAM_Register_Area ram_register_area_75 (
    .bus_out(out), .x(n4x16_decoder_2_out_15), .bus_in(in), .s(s), .e(e), .y(n4x16_decoder_1_out_9));
  RAM_Register_Area ram_register_area_76 (
    .bus_out(out), .x(n4x16_decoder_2_out_16), .bus_in(in), .s(s), .e(e), .y(n4x16_decoder_1_out_9));
  RAM_Register_Area ram_register_area_77 (
    .bus_out(out), .x(n4x16_decoder_2_out_17), .bus_in(in), .s(s), .e(e), .y(n4x16_decoder_1_out_9));
  RAM_Register_Area ram_register_area_78 (
    .bus_out(out), .x(n4x16_decoder_2_out_18), .bus_in(in), .s(s), .e(e), .y(n4x16_decoder_1_out_9));
  RAM_Register_Area ram_register_area_79 (
    .bus_out(out), .x(n4x16_decoder_2_out_19), .bus_in(in), .s(s), .e(e), .y(n4x16_decoder_1_out_9));
  RAM_Register_Area ram_register_area_80 (
    .bus_out(out), .x(n4x16_decoder_2_out_20), .bus_in(in), .s(s), .e(e), .y(n4x16_decoder_1_out_9));
  RAM_Register_Area ram_register_area_81 (
    .bus_out(out), .x(n4x16_decoder_2_out_5), .bus_in(in), .s(s), .e(e), .y(n4x16_decoder_1_out_10));
  RAM_Register_Area ram_register_area_82 (
    .bus_out(out), .x(n4x16_decoder_2_out_6), .bus_in(in), .s(s), .e(e), .y(n4x16_decoder_1_out_10));
  RAM_Register_Area ram_register_area_83 (
    .bus_out(out), .x(n4x16_decoder_2_out_7), .bus_in(in), .s(s), .e(e), .y(n4x16_decoder_1_out_10));
  RAM_Register_Area ram_register_area_84 (
    .bus_out(out), .x(n4x16_decoder_2_out_8), .bus_in(in), .s(s), .e(e), .y(n4x16_decoder_1_out_10));
  RAM_Register_Area ram_register_area_85 (
    .bus_out(out), .x(n4x16_decoder_2_out_9), .bus_in(in), .s(s), .e(e), .y(n4x16_decoder_1_out_10));
  RAM_Register_Area ram_register_area_86 (
    .bus_out(out), .x(n4x16_decoder_2_out_10), .bus_in(in), .s(s), .e(e), .y(n4x16_decoder_1_out_10));
  RAM_Register_Area ram_register_area_87 (
    .bus_out(out), .x(n4x16_decoder_2_out_11), .bus_in(in), .s(s), .e(e), .y(n4x16_decoder_1_out_10));
  RAM_Register_Area ram_register_area_88 (
    .bus_out(out), .x(n4x16_decoder_2_out_12), .bus_in(in), .s(s), .e(e));  // open: y
  RAM_Register_Area ram_register_area_89 (
    .bus_out(out), .x(n4x16_decoder_2_out_13), .bus_in(in), .s(s), .e(e), .y(n4x16_decoder_1_out_10));
  RAM_Register_Area ram_register_area_90 (
    .bus_out(out), .x(n4x16_decoder_2_out_14), .bus_in(in), .s(s), .e(e), .y(n4x16_decoder_1_out_10));
  RAM_Register_Area ram_register_area_91 (
    .bus_out(out), .x(n4x16_decoder_2_out_15), .bus_in(in), .s(s), .e(e), .y(n4x16_decoder_1_out_10));
  RAM_Register_Area ram_register_area_92 (
    .bus_out(out), .x(n4x16_decoder_2_out_16), .bus_in(in), .s(s), .e(e), .y(n4x16_decoder_1_out_10));
  RAM_Register_Area ram_register_area_93 (
    .bus_out(out), .x(n4x16_decoder_2_out_17), .bus_in(in), .s(s), .e(e), .y(n4x16_decoder_1_out_10));
  RAM_Register_Area ram_register_area_94 (
    .bus_out(out), .x(n4x16_decoder_2_out_18), .bus_in(in), .s(s), .e(e), .y(n4x16_decoder_1_out_10));
  RAM_Register_Area ram_register_area_95 (
    .bus_out(out), .x(n4x16_decoder_2_out_19), .bus_in(in), .s(s), .e(e), .y(n4x16_decoder_1_out_10));
  RAM_Register_Area ram_register_area_96 (
    .bus_out(out), .x(n4x16_decoder_2_out_20), .bus_in(in), .s(s), .e(e), .y(n4x16_decoder_1_out_10));
  RAM_Register_Area ram_register_area_97 (
    .bus_out(out), .x(n4x16_decoder_2_out_5), .bus_in(in), .s(s), .e(e), .y(n4x16_decoder_1_out_11));
  RAM_Register_Area ram_register_area_98 (
    .bus_out(out), .x(n4x16_decoder_2_out_6), .bus_in(in), .s(s), .e(e), .y(n4x16_decoder_1_out_11));
  RAM_Register_Area ram_register_area_99 (
    .bus_out(out), .x(n4x16_decoder_2_out_7), .bus_in(in), .s(s), .e(e), .y(n4x16_decoder_1_out_11));
  RAM_Register_Area ram_register_area_100 (
    .bus_out(out), .x(n4x16_decoder_2_out_8), .bus_in(in), .s(s), .e(e), .y(n4x16_decoder_1_out_11));
  RAM_Register_Area ram_register_area_101 (
    .bus_out(out), .x(n4x16_decoder_2_out_9), .bus_in(in), .s(s), .e(e), .y(n4x16_decoder_1_out_11));
  RAM_Register_Area ram_register_area_102 (
    .bus_out(out), .x(n4x16_decoder_2_out_10), .bus_in(in), .s(s), .e(e), .y(n4x16_decoder_1_out_11));
  RAM_Register_Area ram_register_area_103 (
    .bus_out(out), .x(n4x16_decoder_2_out_11), .bus_in(in), .s(s), .e(e), .y(n4x16_decoder_1_out_11));
  RAM_Register_Area ram_register_area_104 (
    .bus_out(out), .x(n4x16_decoder_2_out_12), .bus_in(in), .s(s), .e(e), .y(n4x16_decoder_1_out_11));
  RAM_Register_Area ram_register_area_105 (
    .bus_out(out), .x(n4x16_decoder_2_out_13), .bus_in(in), .s(s), .e(e), .y(n4x16_decoder_1_out_11));
  RAM_Register_Area ram_register_area_106 (
    .bus_out(out), .x(n4x16_decoder_2_out_14), .bus_in(in), .s(s), .e(e), .y(n4x16_decoder_1_out_11));
  RAM_Register_Area ram_register_area_107 (
    .bus_out(out), .x(n4x16_decoder_2_out_15), .bus_in(in), .s(s), .e(e), .y(n4x16_decoder_1_out_11));
  RAM_Register_Area ram_register_area_108 (
    .bus_out(out), .x(n4x16_decoder_2_out_16), .bus_in(in), .s(s), .e(e), .y(n4x16_decoder_1_out_11));
  RAM_Register_Area ram_register_area_109 (
    .bus_out(out), .x(n4x16_decoder_2_out_17), .bus_in(in), .s(s), .e(e), .y(n4x16_decoder_1_out_11));
  RAM_Register_Area ram_register_area_110 (
    .bus_out(out), .x(n4x16_decoder_2_out_18), .bus_in(in), .s(s), .e(e), .y(n4x16_decoder_1_out_11));
  RAM_Register_Area ram_register_area_111 (
    .bus_out(out), .x(n4x16_decoder_2_out_19), .bus_in(in), .s(s), .e(e), .y(n4x16_decoder_1_out_11));
  RAM_Register_Area ram_register_area_112 (
    .bus_out(out), .x(n4x16_decoder_2_out_20), .bus_in(in), .s(s), .e(e), .y(n4x16_decoder_1_out_11));
  RAM_Register_Area ram_register_area_113 (
    .bus_out(out), .x(n4x16_decoder_2_out_5), .bus_in(in), .s(s), .e(e), .y(n4x16_decoder_1_out_12));
  RAM_Register_Area ram_register_area_114 (
    .bus_out(out), .x(n4x16_decoder_2_out_6), .bus_in(in), .s(s), .e(e), .y(n4x16_decoder_1_out_12));
  RAM_Register_Area ram_register_area_115 (
    .bus_out(out), .x(n4x16_decoder_2_out_7), .bus_in(in), .s(s), .e(e), .y(n4x16_decoder_1_out_12));
  RAM_Register_Area ram_register_area_116 (
    .bus_out(out), .x(n4x16_decoder_2_out_8), .bus_in(in), .s(s), .e(e), .y(n4x16_decoder_1_out_12));
  RAM_Register_Area ram_register_area_117 (
    .bus_out(out), .x(n4x16_decoder_2_out_9), .bus_in(in), .s(s), .e(e), .y(n4x16_decoder_1_out_12));
  RAM_Register_Area ram_register_area_118 (
    .bus_out(out), .x(n4x16_decoder_2_out_10), .bus_in(in), .s(s), .e(e), .y(n4x16_decoder_1_out_12));
  RAM_Register_Area ram_register_area_119 (
    .bus_out(out), .x(n4x16_decoder_2_out_11), .bus_in(in), .s(s), .e(e), .y(n4x16_decoder_1_out_12));
  RAM_Register_Area ram_register_area_120 (
    .bus_out(out), .x(n4x16_decoder_2_out_12), .bus_in(in), .s(s), .e(e), .y(n4x16_decoder_1_out_12));
  RAM_Register_Area ram_register_area_121 (
    .bus_out(out), .x(n4x16_decoder_2_out_13), .bus_in(in), .s(s), .e(e), .y(n4x16_decoder_1_out_12));
  RAM_Register_Area ram_register_area_122 (
    .bus_out(out), .x(n4x16_decoder_2_out_14), .bus_in(in), .s(s), .e(e), .y(n4x16_decoder_1_out_12));
  RAM_Register_Area ram_register_area_123 (
    .bus_out(out), .x(n4x16_decoder_2_out_15), .bus_in(in), .s(s), .e(e), .y(n4x16_decoder_1_out_12));
  RAM_Register_Area ram_register_area_124 (
    .bus_out(out), .x(n4x16_decoder_2_out_16), .bus_in(in), .s(s), .e(e), .y(n4x16_decoder_1_out_12));
  RAM_Register_Area ram_register_area_125 (
    .bus_out(out), .x(n4x16_decoder_2_out_17), .bus_in(in), .s(s), .e(e), .y(n4x16_decoder_1_out_12));
  RAM_Register_Area ram_register_area_126 (
    .bus_out(out), .x(n4x16_decoder_2_out_18), .bus_in(in), .s(s), .e(e), .y(n4x16_decoder_1_out_12));
  RAM_Register_Area ram_register_area_127 (
    .bus_out(out), .x(n4x16_decoder_2_out_19), .bus_in(in), .s(s), .e(e), .y(n4x16_decoder_1_out_12));
  RAM_Register_Area ram_register_area_128 (
    .bus_out(out), .x(n4x16_decoder_2_out_20), .bus_in(in), .s(s), .e(e), .y(n4x16_decoder_1_out_12));
  RAM_Register_Area ram_register_area_129 (
    .bus_out(out), .x(n4x16_decoder_2_out_5), .bus_in(in), .s(s), .e(e), .y(n4x16_decoder_1_out_13));
  RAM_Register_Area ram_register_area_130 (
    .bus_out(out), .x(n4x16_decoder_2_out_6), .bus_in(in), .s(s), .e(e), .y(n4x16_decoder_1_out_13));
  RAM_Register_Area ram_register_area_131 (
    .bus_out(out), .x(n4x16_decoder_2_out_7), .bus_in(in), .s(s), .e(e), .y(n4x16_decoder_1_out_13));
  RAM_Register_Area ram_register_area_132 (
    .bus_out(out), .x(n4x16_decoder_2_out_8), .bus_in(in), .s(s), .e(e), .y(n4x16_decoder_1_out_13));
  RAM_Register_Area ram_register_area_133 (
    .bus_out(out), .x(n4x16_decoder_2_out_9), .bus_in(in), .s(s), .e(e), .y(n4x16_decoder_1_out_13));
  RAM_Register_Area ram_register_area_134 (
    .bus_out(out), .x(n4x16_decoder_2_out_10), .bus_in(in), .s(s), .e(e), .y(n4x16_decoder_1_out_13));
  RAM_Register_Area ram_register_area_135 (
    .bus_out(out), .x(n4x16_decoder_2_out_11), .bus_in(in), .s(s), .e(e), .y(n4x16_decoder_1_out_13));
  RAM_Register_Area ram_register_area_136 (
    .bus_out(out), .x(n4x16_decoder_2_out_12), .bus_in(in), .s(s), .e(e), .y(n4x16_decoder_1_out_13));
  RAM_Register_Area ram_register_area_137 (
    .bus_out(out), .x(n4x16_decoder_2_out_13), .bus_in(in), .s(s), .e(e), .y(n4x16_decoder_1_out_13));
  RAM_Register_Area ram_register_area_138 (
    .bus_out(out), .x(n4x16_decoder_2_out_14), .bus_in(in), .s(s), .e(e), .y(n4x16_decoder_1_out_13));
  RAM_Register_Area ram_register_area_139 (
    .bus_out(out), .x(n4x16_decoder_2_out_15), .bus_in(in), .s(s), .e(e), .y(n4x16_decoder_1_out_13));
  RAM_Register_Area ram_register_area_140 (
    .bus_out(out), .x(n4x16_decoder_2_out_16), .bus_in(in), .s(s), .e(e), .y(n4x16_decoder_1_out_13));
  RAM_Register_Area ram_register_area_141 (
    .bus_out(out), .x(n4x16_decoder_2_out_17), .bus_in(in), .s(s), .e(e), .y(n4x16_decoder_1_out_13));
  RAM_Register_Area ram_register_area_142 (
    .bus_out(out), .x(n4x16_decoder_2_out_18), .bus_in(in), .s(s), .e(e), .y(n4x16_decoder_1_out_13));
  RAM_Register_Area ram_register_area_143 (
    .bus_out(out), .x(n4x16_decoder_2_out_19), .bus_in(in), .s(s), .e(e), .y(n4x16_decoder_1_out_13));
  RAM_Register_Area ram_register_area_144 (
    .bus_out(out), .x(n4x16_decoder_2_out_20), .bus_in(in), .s(s), .e(e), .y(n4x16_decoder_1_out_13));
  RAM_Register_Area ram_register_area_145 (
    .bus_out(out), .x(n4x16_decoder_2_out_5), .bus_in(in), .s(s), .e(e), .y(n4x16_decoder_1_out_14));
  RAM_Register_Area ram_register_area_146 (
    .bus_out(out), .x(n4x16_decoder_2_out_6), .bus_in(in), .s(s), .e(e), .y(n4x16_decoder_1_out_14));
  RAM_Register_Area ram_register_area_147 (
    .bus_out(out), .x(n4x16_decoder_2_out_7), .bus_in(in), .s(s), .e(e), .y(n4x16_decoder_1_out_14));
  RAM_Register_Area ram_register_area_148 (
    .bus_out(out), .x(n4x16_decoder_2_out_8), .bus_in(in), .s(s), .e(e), .y(n4x16_decoder_1_out_14));
  RAM_Register_Area ram_register_area_149 (
    .bus_out(out), .x(n4x16_decoder_2_out_9), .bus_in(in), .s(s), .e(e), .y(n4x16_decoder_1_out_14));
  RAM_Register_Area ram_register_area_150 (
    .bus_out(out), .x(n4x16_decoder_2_out_10), .bus_in(in), .s(s), .e(e), .y(n4x16_decoder_1_out_14));
  RAM_Register_Area ram_register_area_151 (
    .bus_out(out), .x(n4x16_decoder_2_out_11), .bus_in(in), .s(s), .e(e), .y(n4x16_decoder_1_out_14));
  RAM_Register_Area ram_register_area_152 (
    .bus_out(out), .x(n4x16_decoder_2_out_12), .bus_in(in), .s(s), .e(e), .y(n4x16_decoder_1_out_14));
  RAM_Register_Area ram_register_area_153 (
    .bus_out(out), .x(n4x16_decoder_2_out_13), .bus_in(in), .s(s), .e(e), .y(n4x16_decoder_1_out_14));
  RAM_Register_Area ram_register_area_154 (
    .bus_out(out), .x(n4x16_decoder_2_out_14), .bus_in(in), .s(s), .e(e), .y(n4x16_decoder_1_out_14));
  RAM_Register_Area ram_register_area_155 (
    .bus_out(out), .x(n4x16_decoder_2_out_15), .bus_in(in), .s(s), .e(e), .y(n4x16_decoder_1_out_14));
  RAM_Register_Area ram_register_area_156 (
    .bus_out(out), .x(n4x16_decoder_2_out_16), .bus_in(in), .s(s), .e(e), .y(n4x16_decoder_1_out_14));
  RAM_Register_Area ram_register_area_157 (
    .bus_out(out), .x(n4x16_decoder_2_out_17), .bus_in(in), .s(s), .e(e), .y(n4x16_decoder_1_out_14));
  RAM_Register_Area ram_register_area_158 (
    .bus_out(out), .x(n4x16_decoder_2_out_18), .bus_in(in), .s(s), .e(e), .y(n4x16_decoder_1_out_14));
  RAM_Register_Area ram_register_area_159 (
    .bus_out(out), .x(n4x16_decoder_2_out_19), .bus_in(in), .s(s), .e(e), .y(n4x16_decoder_1_out_14));
  RAM_Register_Area ram_register_area_160 (
    .bus_out(out), .x(n4x16_decoder_2_out_20), .bus_in(in), .s(s), .e(e), .y(n4x16_decoder_1_out_14));
  RAM_Register_Area ram_register_area_161 (
    .bus_out(out), .x(n4x16_decoder_2_out_5), .bus_in(in), .s(s), .e(e), .y(n4x16_decoder_1_out_15));
  RAM_Register_Area ram_register_area_162 (
    .bus_out(out), .x(n4x16_decoder_2_out_6), .bus_in(in), .s(s), .e(e), .y(n4x16_decoder_1_out_15));
  RAM_Register_Area ram_register_area_163 (
    .bus_out(out), .x(n4x16_decoder_2_out_7), .bus_in(in), .s(s), .e(e), .y(n4x16_decoder_1_out_15));
  RAM_Register_Area ram_register_area_164 (
    .bus_out(out), .x(n4x16_decoder_2_out_8), .bus_in(in), .s(s), .e(e), .y(n4x16_decoder_1_out_15));
  RAM_Register_Area ram_register_area_165 (
    .bus_out(out), .x(n4x16_decoder_2_out_9), .bus_in(in), .s(s), .e(e), .y(n4x16_decoder_1_out_15));
  RAM_Register_Area ram_register_area_166 (
    .bus_out(out), .x(n4x16_decoder_2_out_10), .s(s), .e(e), .y(n4x16_decoder_1_out_15));  // open: bus_in
  RAM_Register_Area ram_register_area_167 (
    .bus_out(out), .x(n4x16_decoder_2_out_11), .bus_in(in), .s(s), .e(e), .y(n4x16_decoder_1_out_15));
  RAM_Register_Area ram_register_area_168 (
    .bus_out(out), .x(n4x16_decoder_2_out_12), .bus_in(in), .s(s), .e(e), .y(n4x16_decoder_1_out_15));
  RAM_Register_Area ram_register_area_169 (
    .bus_out(out), .x(n4x16_decoder_2_out_13), .bus_in(in), .s(s), .e(e), .y(n4x16_decoder_1_out_15));
  RAM_Register_Area ram_register_area_170 (
    .bus_out(out), .x(n4x16_decoder_2_out_14), .bus_in(in), .s(s), .e(e), .y(n4x16_decoder_1_out_15));
  RAM_Register_Area ram_register_area_171 (
    .bus_out(out), .x(n4x16_decoder_2_out_15), .bus_in(in), .s(s), .e(e), .y(n4x16_decoder_1_out_15));
  RAM_Register_Area ram_register_area_172 (
    .bus_out(out), .x(n4x16_decoder_2_out_16), .bus_in(in), .s(s), .e(e), .y(n4x16_decoder_1_out_15));
  RAM_Register_Area ram_register_area_173 (
    .bus_out(out), .x(n4x16_decoder_2_out_17), .bus_in(in), .s(s), .e(e), .y(n4x16_decoder_1_out_15));
  RAM_Register_Area ram_register_area_174 (
    .bus_out(out), .x(n4x16_decoder_2_out_18), .bus_in(in), .s(s), .e(e), .y(n4x16_decoder_1_out_15));
  RAM_Register_Area ram_register_area_175 (
    .bus_out(out), .x(n4x16_decoder_2_out_19), .bus_in(in), .s(s), .e(e), .y(n4x16_decoder_1_out_15));
  RAM_Register_Area ram_register_area_176 (
    .bus_out(out), .x(n4x16_decoder_2_out_20), .bus_in(in), .s(s), .e(e), .y(n4x16_decoder_1_out_15));
  RAM_Register_Area ram_register_area_177 (
    .bus_out(out), .x(n4x16_decoder_2_out_5), .bus_in(in), .s(s), .e(e), .y(n4x16_decoder_1_out_16));
  RAM_Register_Area ram_register_area_178 (
    .bus_out(out), .x(n4x16_decoder_2_out_6), .bus_in(in), .s(s), .e(e), .y(n4x16_decoder_1_out_16));
  RAM_Register_Area ram_register_area_179 (
    .bus_out(out), .x(n4x16_decoder_2_out_7), .bus_in(in), .s(s), .e(e), .y(n4x16_decoder_1_out_16));
  RAM_Register_Area ram_register_area_180 (
    .bus_out(out), .x(n4x16_decoder_2_out_8), .bus_in(in), .s(s), .e(e), .y(n4x16_decoder_1_out_16));
  RAM_Register_Area ram_register_area_181 (
    .bus_out(out), .x(n4x16_decoder_2_out_9), .bus_in(in), .s(s), .e(e), .y(n4x16_decoder_1_out_16));
  RAM_Register_Area ram_register_area_182 (
    .bus_out(out), .x(n4x16_decoder_2_out_10), .bus_in(in), .s(s), .e(e), .y(n4x16_decoder_1_out_16));
  RAM_Register_Area ram_register_area_183 (
    .bus_out(out), .x(n4x16_decoder_2_out_11), .bus_in(in), .s(s), .e(e), .y(n4x16_decoder_1_out_16));
  RAM_Register_Area ram_register_area_184 (
    .bus_out(out), .x(n4x16_decoder_2_out_12), .bus_in(in), .s(s), .e(e), .y(n4x16_decoder_1_out_16));
  RAM_Register_Area ram_register_area_185 (
    .bus_out(out), .x(n4x16_decoder_2_out_13), .bus_in(in), .s(s), .e(e), .y(n4x16_decoder_1_out_16));
  RAM_Register_Area ram_register_area_186 (
    .bus_out(out), .x(n4x16_decoder_2_out_14), .bus_in(in), .s(s), .e(e), .y(n4x16_decoder_1_out_16));
  RAM_Register_Area ram_register_area_187 (
    .bus_out(out), .x(n4x16_decoder_2_out_15), .bus_in(in), .s(s), .e(e), .y(n4x16_decoder_1_out_16));
  RAM_Register_Area ram_register_area_188 (
    .bus_out(out), .x(n4x16_decoder_2_out_16), .bus_in(in), .s(s), .e(e), .y(n4x16_decoder_1_out_16));
  RAM_Register_Area ram_register_area_189 (
    .bus_out(out), .x(n4x16_decoder_2_out_17), .bus_in(in), .s(s), .e(e), .y(n4x16_decoder_1_out_16));
  RAM_Register_Area ram_register_area_190 (
    .bus_out(out), .x(n4x16_decoder_2_out_18), .bus_in(in), .s(s), .e(e), .y(n4x16_decoder_1_out_16));
  RAM_Register_Area ram_register_area_191 (
    .bus_out(out), .x(n4x16_decoder_2_out_19), .bus_in(in), .s(s), .e(e), .y(n4x16_decoder_1_out_16));
  RAM_Register_Area ram_register_area_192 (
    .bus_out(out), .x(n4x16_decoder_2_out_20), .bus_in(in), .s(s), .e(e), .y(n4x16_decoder_1_out_16));
  RAM_Register_Area ram_register_area_193 (
    .bus_out(out), .x(n4x16_decoder_2_out_5), .bus_in(in), .s(s), .e(e), .y(n4x16_decoder_1_out_17));
  RAM_Register_Area ram_register_area_194 (
    .bus_out(out), .x(n4x16_decoder_2_out_6), .bus_in(in), .s(s), .e(e), .y(n4x16_decoder_1_out_17));
  RAM_Register_Area ram_register_area_195 (
    .bus_out(out), .x(n4x16_decoder_2_out_7), .bus_in(in), .s(s), .e(e), .y(n4x16_decoder_1_out_17));
  RAM_Register_Area ram_register_area_196 (
    .bus_out(out), .x(n4x16_decoder_2_out_8), .bus_in(in), .s(s), .e(e), .y(n4x16_decoder_1_out_17));
  RAM_Register_Area ram_register_area_197 (
    .bus_out(out), .x(n4x16_decoder_2_out_9), .bus_in(in), .s(s), .e(e), .y(n4x16_decoder_1_out_17));
  RAM_Register_Area ram_register_area_198 (
    .bus_out(out), .x(n4x16_decoder_2_out_10), .bus_in(in), .s(s), .e(e), .y(n4x16_decoder_1_out_17));
  RAM_Register_Area ram_register_area_199 (
    .bus_out(out), .x(n4x16_decoder_2_out_11), .bus_in(in), .s(s), .e(e), .y(n4x16_decoder_1_out_17));
  RAM_Register_Area ram_register_area_200 (
    .bus_out(out), .x(n4x16_decoder_2_out_12), .bus_in(in), .s(s), .e(e), .y(n4x16_decoder_1_out_17));
  RAM_Register_Area ram_register_area_201 (
    .bus_out(out), .x(n4x16_decoder_2_out_13), .bus_in(in), .s(s), .e(e), .y(n4x16_decoder_1_out_17));
  RAM_Register_Area ram_register_area_202 (
    .bus_out(out), .x(n4x16_decoder_2_out_14), .bus_in(in), .s(s), .e(e), .y(n4x16_decoder_1_out_17));
  RAM_Register_Area ram_register_area_203 (
    .bus_out(out), .x(n4x16_decoder_2_out_15), .bus_in(in), .s(s), .e(e), .y(n4x16_decoder_1_out_17));
  RAM_Register_Area ram_register_area_204 (
    .bus_out(out), .x(n4x16_decoder_2_out_16), .bus_in(in), .s(s), .e(e), .y(n4x16_decoder_1_out_17));
  RAM_Register_Area ram_register_area_205 (
    .bus_out(out), .x(n4x16_decoder_2_out_17), .bus_in(in), .s(s), .e(e), .y(n4x16_decoder_1_out_17));
  RAM_Register_Area ram_register_area_206 (
    .bus_out(out), .x(n4x16_decoder_2_out_18), .bus_in(in), .s(s), .e(e), .y(n4x16_decoder_1_out_17));
  RAM_Register_Area ram_register_area_207 (
    .bus_out(out), .x(n4x16_decoder_2_out_19), .bus_in(in), .s(s), .e(e), .y(n4x16_decoder_1_out_17));
  RAM_Register_Area ram_register_area_208 (
    .bus_out(out), .x(n4x16_decoder_2_out_20), .bus_in(in), .s(s), .e(e), .y(n4x16_decoder_1_out_17));
  RAM_Register_Area ram_register_area_209 (
    .bus_out(out), .x(n4x16_decoder_2_out_5), .bus_in(in), .s(s), .e(e), .y(n4x16_decoder_1_out_18));
  RAM_Register_Area ram_register_area_210 (
    .bus_out(out), .x(n4x16_decoder_2_out_6), .bus_in(in), .s(s), .e(e), .y(n4x16_decoder_1_out_18));
  RAM_Register_Area ram_register_area_211 (
    .bus_out(out), .x(n4x16_decoder_2_out_7), .bus_in(in), .s(s), .e(e), .y(n4x16_decoder_1_out_18));
  RAM_Register_Area ram_register_area_212 (
    .bus_out(out), .x(n4x16_decoder_2_out_8), .bus_in(in), .s(s), .e(e), .y(n4x16_decoder_1_out_18));
  RAM_Register_Area ram_register_area_213 (
    .bus_out(out), .x(n4x16_decoder_2_out_9), .bus_in(in), .s(s), .e(e), .y(n4x16_decoder_1_out_18));
  RAM_Register_Area ram_register_area_214 (
    .bus_out(out), .x(n4x16_decoder_2_out_10), .bus_in(in), .s(s), .e(e), .y(n4x16_decoder_1_out_18));
  RAM_Register_Area ram_register_area_215 (
    .bus_out(out), .x(n4x16_decoder_2_out_11), .bus_in(in), .s(s), .e(e), .y(n4x16_decoder_1_out_18));
  RAM_Register_Area ram_register_area_216 (
    .bus_out(out), .x(n4x16_decoder_2_out_12), .bus_in(in), .s(s), .e(e), .y(n4x16_decoder_1_out_18));
  RAM_Register_Area ram_register_area_217 (
    .bus_out(out), .x(n4x16_decoder_2_out_13), .bus_in(in), .s(s), .e(e), .y(n4x16_decoder_1_out_18));
  RAM_Register_Area ram_register_area_218 (
    .bus_out(out), .x(n4x16_decoder_2_out_14), .bus_in(in), .s(s), .e(e), .y(n4x16_decoder_1_out_18));
  RAM_Register_Area ram_register_area_219 (
    .bus_out(out), .x(n4x16_decoder_2_out_15), .bus_in(in), .s(s), .e(e), .y(n4x16_decoder_1_out_18));
  RAM_Register_Area ram_register_area_220 (
    .bus_out(out), .x(n4x16_decoder_2_out_16), .bus_in(in), .s(s), .e(e), .y(n4x16_decoder_1_out_18));
  RAM_Register_Area ram_register_area_221 (
    .bus_out(out), .x(n4x16_decoder_2_out_17), .bus_in(in), .s(s), .e(e), .y(n4x16_decoder_1_out_18));
  RAM_Register_Area ram_register_area_222 (
    .bus_out(out), .x(n4x16_decoder_2_out_18), .bus_in(in), .s(s), .e(e), .y(n4x16_decoder_1_out_18));
  RAM_Register_Area ram_register_area_223 (
    .bus_out(out), .x(n4x16_decoder_2_out_19), .bus_in(in), .s(s), .e(e), .y(n4x16_decoder_1_out_18));
  RAM_Register_Area ram_register_area_224 (
    .bus_out(out), .x(n4x16_decoder_2_out_20), .bus_in(in), .s(s), .e(e), .y(n4x16_decoder_1_out_18));
  RAM_Register_Area ram_register_area_225 (
    .bus_out(out), .x(n4x16_decoder_2_out_5), .bus_in(in), .s(s), .e(e), .y(n4x16_decoder_1_out_19));
  RAM_Register_Area ram_register_area_226 (
    .bus_out(out), .x(n4x16_decoder_2_out_6), .bus_in(in), .s(s), .e(e), .y(n4x16_decoder_1_out_19));
  RAM_Register_Area ram_register_area_227 (
    .bus_out(out), .x(n4x16_decoder_2_out_7), .bus_in(in), .s(s), .e(e), .y(n4x16_decoder_1_out_19));
  RAM_Register_Area ram_register_area_228 (
    .bus_out(out), .x(n4x16_decoder_2_out_8), .bus_in(in), .s(s), .e(e), .y(n4x16_decoder_1_out_19));
  RAM_Register_Area ram_register_area_229 (
    .bus_out(out), .x(n4x16_decoder_2_out_9), .bus_in(in), .s(s), .e(e), .y(n4x16_decoder_1_out_19));
  RAM_Register_Area ram_register_area_230 (
    .bus_out(out), .x(n4x16_decoder_2_out_10), .bus_in(in), .s(s), .e(e), .y(n4x16_decoder_1_out_19));
  RAM_Register_Area ram_register_area_231 (
    .bus_out(out), .x(n4x16_decoder_2_out_11), .bus_in(in), .s(s), .e(e), .y(n4x16_decoder_1_out_19));
  RAM_Register_Area ram_register_area_232 (
    .bus_out(out), .x(n4x16_decoder_2_out_12), .bus_in(in), .s(s), .e(e), .y(n4x16_decoder_1_out_19));
  RAM_Register_Area ram_register_area_233 (
    .bus_out(out), .x(n4x16_decoder_2_out_13), .bus_in(in), .s(s), .e(e), .y(n4x16_decoder_1_out_19));
  RAM_Register_Area ram_register_area_234 (
    .bus_out(out), .x(n4x16_decoder_2_out_14), .bus_in(in), .s(s), .e(e), .y(n4x16_decoder_1_out_19));
  RAM_Register_Area ram_register_area_235 (
    .bus_out(out), .x(n4x16_decoder_2_out_15), .bus_in(in), .s(s), .e(e), .y(n4x16_decoder_1_out_19));
  RAM_Register_Area ram_register_area_236 (
    .bus_out(out), .x(n4x16_decoder_2_out_16), .bus_in(in), .s(s), .e(e), .y(n4x16_decoder_1_out_19));
  RAM_Register_Area ram_register_area_237 (
    .bus_out(out), .x(n4x16_decoder_2_out_17), .bus_in(in), .s(s), .e(e), .y(n4x16_decoder_1_out_19));
  RAM_Register_Area ram_register_area_238 (
    .bus_out(out), .x(n4x16_decoder_2_out_18), .bus_in(in), .s(s), .e(e), .y(n4x16_decoder_1_out_19));
  RAM_Register_Area ram_register_area_239 (
    .bus_out(out), .x(n4x16_decoder_2_out_19), .bus_in(in), .s(s), .e(e), .y(n4x16_decoder_1_out_19));
  RAM_Register_Area ram_register_area_240 (
    .bus_out(out), .x(n4x16_decoder_2_out_20), .bus_in(in), .s(s), .e(e), .y(n4x16_decoder_1_out_19));
  RAM_Register_Area ram_register_area_241 (
    .bus_out(out), .x(n4x16_decoder_2_out_5), .bus_in(in), .s(s), .e(e), .y(n4x16_decoder_1_out_20));
  RAM_Register_Area ram_register_area_242 (
    .bus_out(out), .x(n4x16_decoder_2_out_6), .bus_in(in), .s(s), .e(e), .y(n4x16_decoder_1_out_20));
  RAM_Register_Area ram_register_area_243 (
    .bus_out(out), .x(n4x16_decoder_2_out_7), .bus_in(in), .s(s), .e(e), .y(n4x16_decoder_1_out_20));
  RAM_Register_Area ram_register_area_244 (
    .bus_out(out), .x(n4x16_decoder_2_out_8), .bus_in(in), .s(s), .e(e), .y(n4x16_decoder_1_out_20));
  RAM_Register_Area ram_register_area_245 (
    .bus_out(out), .x(n4x16_decoder_2_out_9), .bus_in(in), .s(s), .e(e), .y(n4x16_decoder_1_out_20));
  RAM_Register_Area ram_register_area_246 (
    .bus_out(out), .x(n4x16_decoder_2_out_10), .bus_in(in), .s(s), .e(e), .y(n4x16_decoder_1_out_20));
  RAM_Register_Area ram_register_area_247 (
    .bus_out(out), .x(n4x16_decoder_2_out_11), .bus_in(in), .s(s), .e(e), .y(n4x16_decoder_1_out_20));
  RAM_Register_Area ram_register_area_248 (
    .bus_out(out), .x(n4x16_decoder_2_out_12), .bus_in(in), .s(s), .e(e), .y(n4x16_decoder_1_out_20));
  RAM_Register_Area ram_register_area_249 (
    .bus_out(out), .x(n4x16_decoder_2_out_13), .bus_in(in), .s(s), .e(e), .y(n4x16_decoder_1_out_20));
  RAM_Register_Area ram_register_area_250 (
    .bus_out(out), .x(n4x16_decoder_2_out_14), .bus_in(in), .s(s), .e(e), .y(n4x16_decoder_1_out_20));
  RAM_Register_Area ram_register_area_251 (
    .bus_out(out), .x(n4x16_decoder_2_out_15), .bus_in(in), .s(s), .e(e), .y(n4x16_decoder_1_out_20));
  RAM_Register_Area ram_register_area_252 (
    .bus_out(out), .x(n4x16_decoder_2_out_16), .bus_in(in), .s(s), .e(e), .y(n4x16_decoder_1_out_20));
  RAM_Register_Area ram_register_area_253 (
    .bus_out(out), .x(n4x16_decoder_2_out_17), .bus_in(in), .s(s), .e(e), .y(n4x16_decoder_1_out_20));
  RAM_Register_Area ram_register_area_254 (
    .bus_out(out), .x(n4x16_decoder_2_out_18), .bus_in(in), .s(s), .e(e), .y(n4x16_decoder_1_out_20));
  RAM_Register_Area ram_register_area_255 (
    .bus_out(out), .x(n4x16_decoder_2_out_19), .bus_in(in), .s(s), .e(e), .y(n4x16_decoder_1_out_20));
  RAM_Register_Area ram_register_area_256 (
    .bus_out(out), .x(n4x16_decoder_2_out_20), .bus_in(in), .s(s), .e(e), .y(n4x16_decoder_1_out_20));
endmodule
module ALU (
  input  [7:0] a,
  input  [7:0] b,
  input  carry_in,
  input  in_4,
  input  in_5,
  input  in_6,
  output a_b,
  output a_b_2,
  output zero,
  output [7:0] out_10,
  output carry_out
);

  wire and_1_out, n3x8_decoder_1_out_4, n3x8_decoder_1_out_5, n3x8_decoder_1_out_6, n3x8_decoder_1_out_7,
       n3x8_decoder_1_out_8, n3x8_decoder_1_out_9, n3x8_decoder_1_out_10, n3x8_decoder_1_out_11,
       n8_bit_adder_1_carry_out, n8_bit_shift_left_1_shift_out, n8_bit_shift_right_1_shift_out;
  wire [7:0] n8_bit_adder_1_sum, n8_bit_and_1_out_3, n8_bit_compare_1_c, n8_bit_inverter_1_out_2,
       n8_bit_or_1_out_3, n8_bit_shift_left_1_o, n8_bit_shift_right_1_o;

  _8_bit_Inverter u_8_bit_inverter_1 (.out_2(n8_bit_inverter_1_out_2), .in_1(a));
  _8_bit_Shift_Left u_8_bit_shift_left_1 (
    .shift_out(n8_bit_shift_left_1_shift_out), .o(n8_bit_shift_left_1_o), .i(a), .shift_in(carry_in));
  _8_bit_Shift_Right u_8_bit_shift_right_1 (
    .shift_out(n8_bit_shift_right_1_shift_out), .o(n8_bit_shift_right_1_o), .i(a), .shift_in(carry_in));
  _8_bit_Adder u_8_bit_adder_1 (
    .carry_out(n8_bit_adder_1_carry_out), .sum(n8_bit_adder_1_sum), .a(a), .b(b), .carry_in(carry_in));
  _8_bit_Compare u_8_bit_compare_1 (.a(a), .b(b), .c(n8_bit_compare_1_c), .out_4(a_b), .out_5(a_b_2));
  _8_bit_Or u_8_bit_or_1 (.in_1(a), .in_2(b), .out_3(n8_bit_or_1_out_3));
  _8_bit_And u_8_bit_and_1 (.out_3(n8_bit_and_1_out_3), .in_1(a), .in_2(b));
  _3x8_Decoder u_3x8_decoder_1 (
    .out_4(n3x8_decoder_1_out_4), .out_5(n3x8_decoder_1_out_5), .out_6(n3x8_decoder_1_out_6),
    .out_7(n3x8_decoder_1_out_7), .out_8(n3x8_decoder_1_out_8), .out_9(n3x8_decoder_1_out_9),
    .out_10(n3x8_decoder_1_out_10), .out_11(n3x8_decoder_1_out_11), .a(in_4), .b(in_5), .c(in_6));
  _1_byte_Enabler1 u_1_byte_enabler1_1 (.o(out_10), .i(n8_bit_compare_1_c), .e(n3x8_decoder_1_out_10));
  _1_byte_Enabler1 u_1_byte_enabler1_2 (.o(out_10), .i(n8_bit_or_1_out_3), .e(n3x8_decoder_1_out_9));
  _1_byte_Enabler1 u_1_byte_enabler1_3 (.o(out_10), .i(n8_bit_and_1_out_3), .e(n3x8_decoder_1_out_8));
  _1_byte_Enabler1 u_1_byte_enabler1_4 (.o(out_10), .i(n8_bit_inverter_1_out_2), .e(n3x8_decoder_1_out_7));
  and and_1 (and_1_out, n8_bit_shift_left_1_shift_out, n3x8_decoder_1_out_6);
  _1_byte_Enabler1 u_1_byte_enabler1_5 (.o(out_10), .i(n8_bit_shift_left_1_o), .e(n3x8_decoder_1_out_6));
  and and_2 (carry_out, n8_bit_shift_right_1_shift_out, n3x8_decoder_1_out_5);
  _1_byte_Enabler1 u_1_byte_enabler1_6 (.o(out_10), .i(n8_bit_shift_right_1_o), .e(n3x8_decoder_1_out_5));
  and and_3 (and_1_out, n8_bit_adder_1_carry_out, n3x8_decoder_1_out_4);
  _1_byte_Enabler1 u_1_byte_enabler1_7 (.o(out_10), .i(n8_bit_adder_1_sum), .e(n3x8_decoder_1_out_4));
  _8_bit_Zero u_8_bit_zero_1 (.bus_in(out_10), .zero(zero));
endmodule

module bus1 (
  input  [7:0] in,
  input  bus1,
  output [7:0] out
);

  wire not_1_out;

  and and_1 (out[7], in[7], not_1_out);
  and and_2 (out[6], in[6], not_1_out);
  and and_3 (out[5], in[5], not_1_out);
  and and_4 (out[4], in[4], not_1_out);
  and and_5 (out[3], in[3], not_1_out);
  and and_6 (out[2], in[2], not_1_out);
  and and_7 (out[1], in[1], not_1_out);
  not not_1 (not_1_out, bus1);
  or or_1 (out[0], in[0], bus1);
endmodule

module TMP (
  input  [7:0] i,
  input  s,
  output [7:0] o
);

  _1_byte_Memory u_1_byte_memory_1 (.o(o), .i(i), .s(s));
endmodule

module ACC (
  input  [7:0] i,
  input  s,
  input  e,
  output [7:0] o
);

  wire [7:0] n1_byte_memory_1_o;

  _1_byte_Memory u_1_byte_memory_1 (.o(n1_byte_memory_1_o), .i(i), .s(s));
  _1_byte_Enabler u_1_byte_enabler_1 (.o(o), .i(n1_byte_memory_1_o), .e(e));
endmodule

module Clock (
  output clk,
  output clk_e,
  output clk_s
);

  wire clk_d_out;

  Clock_part #(.highDuration(2), .lowDuration(2), .phaseOffset(1)) u_clk (.out(clk));
  Clock_part #(.highDuration(2), .lowDuration(2)) clk_d (.out(clk_d_out));
  or or_1 (clk_e, clk, clk_d_out);
  and and_1 (clk_s, clk, clk_d_out);
endmodule

module Stepper (
  input  reset,
  input  clk,
  output Step_1,
  output Step_2,
  output Step_3,
  output Step_4,
  output Step_5,
  output Step_6,
  output Step_7
);

  wire M1_o, M2_o, M3_o, M4_o, M5_o, M6_o, M7_o, M8_o, M9_o, M10_o, M11_o, M12_o, not_1_out, not_2_out,
       not_3_out, not_4_out, not_5_out, not_6_out, not_7_out, not_8_out, or_1_out, or_2_out;

  not not_1 (not_1_out, clk);
  not not_2 (not_2_out, reset);
  or or_1 (or_1_out, reset, not_1_out);
  or or_2 (or_2_out, reset, clk);
  or or_3 (Step_1, reset, not_3_out);
  _1_bit_m M1 (.o(M1_o), .i(not_2_out), .s(or_1_out));
  not not_3 (not_3_out, M2_o);
  _1_bit_m M2 (.o(M2_o), .i(M1_o), .s(or_2_out));
  and and_1 (Step_2, M2_o, not_4_out);
  not not_4 (not_4_out, M4_o);
  _1_bit_m M3 (.o(M3_o), .i(M2_o), .s(or_1_out));
  and and_2 (Step_3, M4_o, not_5_out);
  _1_bit_m M4 (.o(M4_o), .i(M3_o), .s(or_2_out));
  not not_5 (not_5_out, M6_o);
  _1_bit_m M5 (.o(M5_o), .i(M4_o), .s(or_1_out));
  and and_3 (Step_4, M6_o, not_6_out);
  _1_bit_m M6 (.o(M6_o), .i(M5_o), .s(or_2_out));
  _1_bit_m M7 (.o(M7_o), .i(M6_o), .s(or_1_out));
  not not_6 (not_6_out, M8_o);
  _1_bit_m M8 (.o(M8_o), .i(M7_o), .s(or_2_out));
  and and_4 (Step_5, M8_o, not_7_out);
  _1_bit_m M9 (.o(M9_o), .i(M8_o), .s(or_1_out));
  not not_7 (not_7_out, M10_o);
  _1_bit_m M10 (.o(M10_o), .i(M9_o), .s(or_2_out));
  and and_5 (Step_6, M10_o, not_8_out);
  not not_8 (not_8_out, M12_o);
  _1_bit_m M11 (.o(M11_o), .i(M10_o), .s(or_1_out));
  nor nor_1 (Step_7, M12_o, 1'b0);
  _1_bit_m M12 (.o(M12_o), .i(M11_o), .s(or_2_out));
endmodule

module Control_Unit (
);

  wire clock_1_clk, clock_1_clk_e, clock_1_clk_s, stepper_1_step_1, stepper_1_step_2, stepper_1_step_3,
       stepper_1_step_4, stepper_1_step_5, stepper_1_step_6, stepper_1_step_7;

  Clock clock_1 (.clk_e(clock_1_clk_e), .clk_s(clock_1_clk_s), .clk(clock_1_clk));
  Stepper stepper_1 (
    .Step_7(stepper_1_step_7), .Step_1(stepper_1_step_1), .Step_2(stepper_1_step_2),
    .Step_3(stepper_1_step_3), .Step_4(stepper_1_step_4), .Step_5(stepper_1_step_5),
    .Step_6(stepper_1_step_6), .reset(stepper_1_step_7), .clk(clock_1_clk));
endmodule

module cpu (
);

  wire undriven, undriven_2, undriven_3, undriven_4, undriven_5, undriven_6, undriven_7, undriven_8;
  wire [7:0] acc_1_o, alu_1_out_10, bus1_1_out, tmp_1_o;

  TMP tmp_1 (.o(tmp_1_o), .s(undriven_5), .i(acc_1_o));
  bus1 bus1_1 (.out(bus1_1_out), .in(tmp_1_o), .bus1(undriven_6));
  ALU alu_1 (
    .out_10(alu_1_out_10), .carry_in(undriven_4), .in_4(undriven), .in_5(undriven_2), .in_6(undriven_3),
    .a(acc_1_o), .b(bus1_1_out));  // open: zero, a_b, a_b_2, carry_out
  ACC acc_1 (.o(acc_1_o), .s(undriven_7), .e(undriven_8), .i(alu_1_out_10));
  _1_byte_Register u_1_byte_register_1 (.o(acc_1_o), .i(acc_1_o));  // open: s, e
  _1_byte_Register u_1_byte_register_2 (.o(acc_1_o), .i(acc_1_o));  // open: s, e
  _1_byte_Register u_1_byte_register_3 (.o(acc_1_o), .i(acc_1_o));  // open: s, e
  _1_byte_Register u_1_byte_register_4 (.o(acc_1_o), .i(acc_1_o));  // open: s, e
  RAM_256 ram_256_1 (.out(acc_1_o), .Address(acc_1_o), .in(acc_1_o));  // open: sa, s, e
endmodule

module Clock2 (
  output clk_s,
  output clk,
  output clk_e
);

  wire clk_raw_out, j_k_ff_1_qn;

  Clock_part clk_raw (.out(clk_raw_out));
  J_K_Flip_Flop j_k_ff_1 (.J(1'b1), .clk(clk_raw_out), .K(1'b1), .Q(clk), .Qn(j_k_ff_1_qn));  // open: preset, reset
  and and_1 (clk_s, clk_raw_out, clk);
  nand nand_1 (clk_e, j_k_ff_1_qn, clk_raw_out);
endmodule
