// Logisim project CPU_BasicGates.circ as structural Verilog: 5 circuits, main circuit NOT
module NOT (
  input  s,
  output o
);

  nand nand_1 (o, s, s);
endmodule

module AND (
  input  a,
  input  b,
  output o
);

  wire nand_1_out;

  nand nand_1 (nand_1_out, a, b);
  nand nand_2 (o, nand_1_out, nand_1_out);
endmodule

module OR (
  input  a,
  input  b,
  output c
);

  wire nand_1_out, nand_2_out;

  nand nand_1 (nand_1_out, a, a);
  nand nand_2 (nand_2_out, b, b);
  nand nand_3 (c, nand_1_out, nand_2_out);
endmodule

module XOR (
  input  a,
  input  b,
  output c
);

  wire nand_1_out, nand_2_out, nand_3_out, nand_4_out;

  nand nand_1 (nand_1_out, a, a);
  nand nand_2 (nand_2_out, b, b);
  nand nand_3 (nand_3_out, nand_1_out, b);
  nand nand_4 (nand_4_out, a, nand_2_out);
  nand nand_5 (c, nand_3_out, nand_4_out);
endmodule

module _3_AND (
  input  a,
  input  b,
  input  c,
  output o
);

  wire and_1_out;

  and and_1 (and_1_out, a, b);
  and and_2 (o, and_1_out, c);
endmodule
