// Logisim project CPU_Decoders.circ as structural Verilog: 5 circuits, main circuit 2x4 Decoder
module _2x4_Decoder (
  input  a,
  input  b,
  output out_3,
  output out_4,
  output out_5,
  output out_6
);

  wire not_1_out, not_2_out;

  not not_1 (not_1_out, b);
  not not_2 (not_2_out, a);
  and and_1 (out_3, not_2_out, not_1_out);
  and and_2 (out_4, not_2_out, b);
  and and_3 (out_5, a, not_1_out);
  and and_4 (out_6, a, b);
endmodule

module _3x8_Decoder (
  input  a,
  input  b,
  input  c,
  output out_4,
  output out_5,
  output out_6,
  output out_7,
  output out_8,
  output out_9,
  output out_10,
  output out_11
);

  wire not_1_out, not_2_out, not_3_out;

  not not_1 (not_1_out, c);
  not not_2 (not_2_out, b);
  not not_3 (not_3_out, a);
  and and_1 (out_4, not_3_out, not_2_out, not_1_out);
  and and_2 (out_5, not_3_out, not_2_out, c);
  and and_3 (out_6, not_3_out, b, not_1_out);
  and and_4 (out_7, not_3_out, b, c);
  and and_5 (out_8, a, not_2_out, not_1_out);
  and and_6 (out_9, a, not_2_out, c);
  and and_7 (out_10, a, b, not_1_out);
  and and_8 (out_11, a, b, c);
endmodule

module _4x16_Decoder (
  input  a,
  input  b,
  input  c,
  input  d,
  output out_5,
  output out_6,
  output out_7,
  output out_8,
  output out_9,
  output out_10,
  output out_11,
  output out_12,
  output out_13,
  output out_14,
  output out_15,
  output out_16,
  output out_17,
  output out_18,
  output out_19,
  output out_20
);

  wire not_1_out, not_2_out, not_3_out, not_4_out;

  not not_1 (not_1_out, d);
  not not_2 (not_2_out, c);
  not not_3 (not_3_out, b);
  not not_4 (not_4_out, a);
  and and_1 (out_5, not_4_out, not_3_out, not_2_out, not_1_out);
  and and_2 (out_6, not_4_out, not_3_out, not_2_out, d);
  and and_3 (out_7, not_4_out, not_3_out, c, not_1_out);
  and and_4 (out_8, not_4_out, not_3_out, c, d);
  and and_5 (out_9, not_4_out, b, not_2_out, not_1_out);
  and and_6 (out_10, not_4_out, b, not_2_out, d);
  and and_7 (out_11, not_4_out, b, c, not_1_out);
  and and_8 (out_12, not_4_out, b, c, d);
  and and_9 (out_13, a, not_3_out, not_2_out, not_1_out);
  and and_10 (out_14, a, not_3_out, not_2_out, d);
  and and_11 (out_15, a, not_3_out, c, not_1_out);
  and and_12 (out_16, a, not_3_out, c, d);
  and and_13 (out_17, a, b, not_2_out, not_1_out);
  and and_14 (out_18, a, b, not_2_out, d);
  and and_15 (out_19, a, b, c, not_1_out);
  and and_16 (out_20, a, b, c, d);
endmodule

module _4x16_Decoder0 (
  input  a,
  input  b,
  input  c,
  input  d,
  output out_5,
  output out_6,
  output out_7,
  output out_8,
  output out_9,
  output out_10,
  output out_11,
  output out_12,
  output out_13,
  output out_14,
  output out_15,
  output out_16,
  output out_17,
  output out_18,
  output out_19,
  output out_20
);

  wire not_1_out, not_2_out, not_3_out, not_4_out;

  not not_1 (not_1_out, d);
  not not_2 (not_2_out, c);
  not not_3 (not_3_out, b);
  not not_4 (not_4_out, a);
  and and_1 (out_5, not_4_out, not_3_out, not_2_out, not_1_out);
  and and_2 (out_6, not_4_out, not_3_out, not_2_out, d);
  and and_3 (out_7, not_4_out, not_3_out, c, not_1_out);
  and and_4 (out_8, not_4_out, not_3_out, c, d);
  and and_5 (out_9, not_4_out, b, not_2_out, not_1_out);
  and and_6 (out_10, not_4_out, b, not_2_out, d);
  and and_7 (out_11, not_4_out, b, c, not_1_out);
  and and_8 (out_12, not_4_out, b, c, d);
  and and_9 (out_13, a, not_3_out, not_2_out, not_1_out);
  and and_10 (out_14, a, not_3_out, not_2_out, d);
  and and_11 (out_15, a, not_3_out, c, not_1_out);
  and and_12 (out_16, a, not_3_out, c, d);
  and and_13 (out_17, a, b, not_2_out, not_1_out);
  and and_14 (out_18, a, b, not_2_out, d);
  and and_15 (out_19, a, b, c, not_1_out);
  and and_16 (out_20, a, b, c, d);
endmodule

module _4x16_Decoder1 (
  input  a,
  input  b,
  input  c,
  input  d,
  output out_5,
  output out_6,
  output out_7,
  output out_8,
  output out_9,
  output out_10,
  output out_11,
  output out_12,
  output out_13,
  output out_14,
  output out_15,
  output out_16,
  output out_17,
  output out_18,
  output out_19,
  output out_20
);

  wire not_1_out, not_2_out, not_3_out, not_4_out;

  not not_1 (not_1_out, d);
  not not_2 (not_2_out, c);
  not not_3 (not_3_out, b);
  not not_4 (not_4_out, a);
  and and_1 (out_5, not_4_out, not_3_out, not_2_out, not_1_out);
  and and_2 (out_6, not_4_out, not_3_out, not_2_out, d);
  and and_3 (out_7, not_4_out, not_3_out, c, not_1_out);
  and and_4 (out_8, not_4_out, not_3_out, c, d);
  and and_5 (out_9, not_4_out, b, not_2_out, not_1_out);
  and and_6 (out_10, not_4_out, b, not_2_out, d);
  and and_7 (out_11, not_4_out, b, c, not_1_out);
  and and_8 (out_12, not_4_out, b, c, d);
  and and_9 (out_13, a, not_3_out, not_2_out, not_1_out);
  and and_10 (out_14, a, not_3_out, not_2_out, d);
  and and_11 (out_15, a, not_3_out, c, not_1_out);
  and and_12 (out_16, a, not_3_out, c, d);
  and and_13 (out_17, a, b, not_2_out, not_1_out);
  and and_14 (out_18, a, b, not_2_out, d);
  and and_15 (out_19, a, b, c, not_1_out);
  and and_16 (out_20, a, b, c, d);
endmodule
