// Logisim project CPU_Memory.circ as structural Verilog: 6 circuits, main circuit 1 bit Memory
module _1_bit_Memory (
  input  i,
  input  s,
  output o
);

  wire nand_1_out, nand_2_out, nand_4_out;

  nand nand_1 (nand_1_out, i, s);
  nand nand_2 (nand_2_out, nand_1_out, s);
  nand nand_3 (o, nand_1_out, nand_4_out);
  nand nand_4 (nand_4_out, o, nand_2_out);
endmodule

module _8_bit_Memory (
  input  i,
  input  i_2,
  input  i_3,
  input  i_4,
  input  i_5,
  input  i_6,
  input  i_7,
  input  i_8,
  input  s,
  output o,
  output o_2,
  output o_3,
  output o_4,
  output o_5,
  output o_6,
  output o_7,
  output o_8
);

  _1_bit_Memory u_1_bit_memory_1 (.o(o), .i(i), .s(s));
  _1_bit_Memory u_1_bit_memory_2 (.o(o_2), .i(i_2), .s(s));
  _1_bit_Memory u_1_bit_memory_3 (.o(o_3), .i(i_3), .s(s));
  _1_bit_Memory u_1_bit_memory_4 (.o(o_4), .i(i_4), .s(s));
  _1_bit_Memory u_1_bit_memory_5 (.o(o_5), .i(i_5), .s(s));
  _1_bit_Memory u_1_bit_memory_6 (.o(o_6), .i(i_6), .s(s));
  _1_bit_Memory u_1_bit_memory_7 (.o(o_7), .i(i_7), .s(s));
  _1_bit_Memory u_1_bit_memory_8 (.o(o_8), .i(i_8), .s(s));
endmodule

module _1_byte_Memory (
  input  [7:0] i,
  input  s,
  output [7:0] o
);

  _1_bit_Memory u_1_bit_memory_1 (.o(o[7]), .i(i[7]), .s(s));
  _1_bit_Memory u_1_bit_memory_2 (.o(o[6]), .i(i[6]), .s(s));
  _1_bit_Memory u_1_bit_memory_3 (.o(o[5]), .i(i[5]), .s(s));
  _1_bit_Memory u_1_bit_memory_4 (.o(o[4]), .i(i[4]), .s(s));
  _1_bit_Memory u_1_bit_memory_5 (.o(o[3]), .i(i[3]), .s(s));
  _1_bit_Memory u_1_bit_memory_6 (.o(o[2]), .i(i[2]), .s(s));
  _1_bit_Memory u_1_bit_memory_7 (.o(o[1]), .i(i[1]), .s(s));
  _1_bit_Memory u_1_bit_memory_8 (.o(o[0]), .i(i[0]), .s(s));
endmodule

module _8_bit_Enabler (
  input  i,
  input  i_2,
  input  i_3,
  input  i_4,
  input  i_5,
  input  i_6,
  input  i_7,
  input  i_8,
  input  e,
  output o,
  output o_2,
  output o_3,
  output o_4,
  output o_5,
  output o_6,
  output o_7,
  output o_8
);

  and and_1 (o, i, e);
  and and_2 (o_2, i_2, e);
  and and_3 (o_3, i_3, e);
  and and_4 (o_4, i_4, e);
  and and_5 (o_5, i_5, e);
  and and_6 (o_6, i_6, e);
  and and_7 (o_7, i_7, e);
  and and_8 (o_8, i_8, e);
endmodule

module _1_byte_Enabler (
  input  [7:0] i,
  input  e,
  output [7:0] o
);

  and and_1 (o[7], i[7], e);
  and and_2 (o[6], i[6], e);
  and and_3 (o[5], i[5], e);
  and and_4 (o[4], i[4], e);
  and and_5 (o[3], i[3], e);
  and and_6 (o[2], i[2], e);
  and and_7 (o[1], i[1], e);
  and and_8 (o[0], i[0], e);
endmodule

module _1_byte_Enabler1 (
  input  [7:0] i,
  input  e,
  output [7:0] o
);

  wire and_1_out, and_2_out, and_3_out, and_4_out, and_5_out, and_6_out, and_7_out, and_8_out;

  and and_1 (and_1_out, i[7], e);
  and and_2 (and_2_out, i[6], e);
  and and_3 (and_3_out, i[5], e);
  and and_4 (and_4_out, i[4], e);
  and and_5 (and_5_out, i[3], e);
  and and_6 (and_6_out, i[2], e);
  and and_7 (and_7_out, i[1], e);
  and and_8 (and_8_out, i[0], e);
  assign o[7] = e ? and_1_out : 1'bz;  // Controlled_Buffer controlled_buffer_1
  assign o[6] = e ? and_2_out : 1'bz;  // Controlled_Buffer controlled_buffer_2
  assign o[5] = e ? and_3_out : 1'bz;  // Controlled_Buffer controlled_buffer_3
  assign o[4] = e ? and_4_out : 1'bz;  // Controlled_Buffer controlled_buffer_4
  assign o[3] = e ? and_5_out : 1'bz;  // Controlled_Buffer controlled_buffer_5
  assign o[2] = e ? and_6_out : 1'bz;  // Controlled_Buffer controlled_buffer_6
  assign o[1] = e ? and_7_out : 1'bz;  // Controlled_Buffer controlled_buffer_7
  assign o[0] = e ? and_8_out : 1'bz;  // Controlled_Buffer controlled_buffer_8
endmodule
