// Logisim project HowDoItKnow.circ as structural Verilog
module NOT (
  input  s,
  output o
);

  nand nand_1 (o, s, s);
endmodule

module AND (
  input  a,
  input  b,
  output o
);

  wire nand_1_out;

  nand nand_1 (nand_1_out, a, b);
  NOT not_1 (.o(o), .s(nand_1_out));
endmodule

module OR (
  input  a,
  input  b,
  output c
);

  wire not_1_out, not_2_out;

  not not_1 (not_1_out, a);
  not not_2 (not_2_out, b);
  nand nand_1 (c, not_1_out, not_2_out);
endmodule

module XOR (
  input  a,
  input  b,
  output c
);

  wire nand_1_out, nand_2_out, not_1_out, not_2_out;

  not not_1 (not_1_out, a);
  not not_2 (not_2_out, b);
  nand nand_1 (nand_1_out, not_1_out, b);
  nand nand_2 (nand_2_out, a, not_2_out);
  nand nand_3 (c, nand_1_out, nand_2_out);
endmodule

module _1_bit_memory (
  input  i,
  input  s,
  output o
);

  wire nand_1_out, nand_2_out, nand_4_out;

  nand nand_1 (nand_1_out, i, s);
  nand nand_2 (nand_2_out, nand_1_out, s);
  nand nand_3 (o, nand_1_out, nand_4_out);
  nand nand_4 (nand_4_out, o, nand_2_out);
endmodule

module _1_bit_m (
  input  i,
  input  s,
  output o
);

  wire _1_out, _2_out, _4_out;

  nand _1 (_1_out, i, s);
  nand _2 (_2_out, _1_out, s);
  nand _3 (o, _1_out, _4_out);
  nand _4 (_4_out, o, _2_out);
endmodule

module _8_bit_memory (
  input  [7:0] i,
  input  s,
  output [7:0] o
);

  _1_bit_memory u_1_bit_memory_1 (.o(o[7]), .i(i[7]), .s(s));
  _1_bit_memory u_1_bit_memory_2 (.o(o[6]), .i(i[6]), .s(s));
  _1_bit_memory u_1_bit_memory_3 (.o(o[5]), .i(i[5]), .s(s));
  _1_bit_memory u_1_bit_memory_4 (.o(o[4]), .i(i[4]), .s(s));
  _1_bit_memory u_1_bit_memory_5 (.o(o[3]), .i(i[3]), .s(s));
  _1_bit_memory u_1_bit_memory_6 (.o(o[2]), .i(i[2]), .s(s));
  _1_bit_memory u_1_bit_memory_7 (.o(o[1]), .i(i[1]), .s(s));
  _1_bit_memory u_1_bit_memory_8 (.o(o[0]), .i(i[0]), .s(s));
endmodule

module Enabler (
  input  [7:0] i,
  input  e,
  output [7:0] o
);

  and and_1 (o[7], i[7], e);
  and and_2 (o[6], i[6], e);
  and and_3 (o[5], i[5], e);
  and and_4 (o[4], i[4], e);
  and and_5 (o[3], i[3], e);
  and and_6 (o[2], i[2], e);
  and and_7 (o[1], i[1], e);
  and and_8 (o[0], i[0], e);
endmodule

module Register (
  input  [7:0] i,
  input  s,
  input  e,
  output [7:0] o
);

  wire [7:0] n8_bit_memory_1_o;

  _8_bit_memory u_8_bit_memory_1 (.i(i), .s(s), .o(n8_bit_memory_1_o));
  Enabler enabler_1 (.i(n8_bit_memory_1_o), .e(e), .o(o));
endmodule

module Register2 (
  input  [7:0] i,
  input  s,
  input  e,
  output [7:0] o
);

  wire [7:0] n8_bit_memory_1_o;

  _8_bit_memory u_8_bit_memory_1 (.i(i), .s(s), .o(n8_bit_memory_1_o));
  Enabler enabler_1 (.i(n8_bit_memory_1_o), .e(e), .o(o));
endmodule

module _3_and (
  input  a,
  input  b,
  input  c,
  output o
);

  wire and_1_out;

  and and_1 (and_1_out, a, b);
  and and_2 (o, and_1_out, c);
endmodule

module _2x4_Decoder (
  input  a,
  input  b,
  output out_3,
  output out_4,
  output out_5,
  output out_6
);

  wire not_1_out, not_2_out;

  not not_1 (not_1_out, b);
  not not_2 (not_2_out, a);
  and and_1 (out_3, not_2_out, not_1_out);
  and and_2 (out_4, not_2_out, b);
  and and_3 (out_5, a, not_1_out);
  and and_4 (out_6, a, b);
endmodule

module _3x8_Decoder (
  input  a,
  input  b,
  input  c,
  output out_4,
  output out_5,
  output out_6,
  output out_7,
  output out_8,
  output out_9,
  output out_10,
  output out_11
);

  wire not_1_out, not_2_out, not_3_out;

  not not_1 (not_1_out, c);
  not not_2 (not_2_out, b);
  not not_3 (not_3_out, a);
  and and_1 (out_4, not_3_out, not_2_out, not_1_out);
  and and_2 (out_5, not_3_out, not_2_out, c);
  and and_3 (out_6, not_3_out, b, not_1_out);
  and and_4 (out_7, not_3_out, b, c);
  and and_5 (out_8, a, not_2_out, not_1_out);
  and and_6 (out_9, a, not_2_out, c);
  and and_7 (out_10, a, b, not_1_out);
  and and_8 (out_11, a, b, c);
endmodule

module test_Register (
  input  in_1,
  input  in_2,
  input  in_3,
  input  in_4,
  input  [7:0] in_5,
  output [7:0] out_6,
  output [7:0] out_7
);

  wire and_1_out, not_1_out, not_2_out;
  wire [7:0] controlled_buffer_1_out;

  not not_1 (not_1_out, in_2);
  not not_2 (not_2_out, in_1);
  and and_1 (and_1_out, not_1_out, not_2_out);
  assign controlled_buffer_1_out = and_1_out ? in_5 : 8'bz;  // Controlled_Buffer controlled_buffer_1
  Register2 R_1 (.o(out_6), .i(controlled_buffer_1_out), .s(in_3), .e(in_1));
  assign controlled_buffer_1_out = in_1 ? out_6 : 8'bz;  // Controlled_Buffer controlled_buffer_2
  Register2 R_2 (.o(out_7), .i(controlled_buffer_1_out), .s(in_4), .e(in_2));
  assign controlled_buffer_1_out = in_2 ? out_7 : 8'bz;  // Controlled_Buffer controlled_buffer_3
endmodule

module Stepper (
  input  reset,
  input  clk,
  output Step_1,
  output Step_2,
  output Step_3,
  output Step_4,
  output Step_5,
  output Step_6,
  output Step_7
);

  wire M1_o, M2_o, M3_o, M4_o, M5_o, M6_o, M7_o, M8_o, M9_o, M10_o, M11_o, not_1_out, not_2_out, not_3_out,
       not_4_out, not_5_out, not_6_out, not_7_out, not_8_out, or_1_out, or_2_out;

  not not_1 (not_1_out, clk);
  not not_2 (not_2_out, reset);
  or or_1 (or_1_out, reset, not_1_out);
  or or_2 (or_2_out, reset, clk);
  or or_3 (Step_1, reset, not_3_out);
  _1_bit_m M1 (.o(M1_o), .i(not_2_out), .s(or_1_out));
  not not_3 (not_3_out, M2_o);
  _1_bit_m M2 (.o(M2_o), .i(M1_o), .s(or_2_out));
  and and_1 (Step_2, M2_o, not_4_out);
  not not_4 (not_4_out, M4_o);
  _1_bit_m M3 (.o(M3_o), .i(M2_o), .s(or_1_out));
  and and_2 (Step_3, M4_o, not_5_out);
  _1_bit_m M4 (.o(M4_o), .i(M3_o), .s(or_2_out));
  not not_5 (not_5_out, M6_o);
  _1_bit_m M5 (.o(M5_o), .i(M4_o), .s(or_1_out));
  and and_3 (Step_4, M6_o, not_6_out);
  _1_bit_m M6 (.o(M6_o), .i(M5_o), .s(or_2_out));
  _1_bit_m M7 (.o(M7_o), .i(M6_o), .s(or_1_out));
  not not_6 (not_6_out, M8_o);
  _1_bit_m M8 (.o(M8_o), .i(M7_o), .s(or_2_out));
  and and_4 (Step_5, M8_o, not_7_out);
  _1_bit_m M9 (.o(M9_o), .i(M8_o), .s(or_1_out));
  not not_7 (not_7_out, M10_o);
  _1_bit_m M10 (.o(M10_o), .i(M9_o), .s(or_2_out));
  and and_5 (Step_6, M10_o, not_8_out);
  not not_8 (not_8_out, Step_7);
  _1_bit_m M11 (.o(M11_o), .i(M10_o), .s(or_1_out));
  _1_bit_m M12 (.o(Step_7), .i(M11_o), .s(or_2_out));
endmodule

module adder (
  input  a,
  input  b,
  input  carry_in,
  output sum,
  output carry_out
);

  wire and_1_out, and_2_out, xor_1_out;

  xor xor_1 (xor_1_out, a, b);
  and and_1 (and_1_out, carry_in, xor_1_out);
  and and_2 (and_2_out, a, b);
  xor xor_2 (sum, xor_1_out, carry_in);
  or or_1 (carry_out, and_1_out, and_2_out);
endmodule

module _8_bit_Adder (
  input  [7:0] a,
  input  [7:0] in_2,
  input  in_3,
  output out_4,
  output [7:0] out_5
);

  wire adder_2_carry_out, adder_3_carry_out, adder_4_carry_out, adder_5_carry_out, adder_6_carry_out,
       adder_7_carry_out, adder_8_carry_out;

  adder adder_1 (.sum(out_5[7]), .carry_out(out_4), .a(a[7]), .b(in_2[7]), .carry_in(adder_2_carry_out));
  adder adder_2 (.sum(out_5[6]), .carry_out(adder_2_carry_out), .a(a[6]), .b(in_2[6]), .carry_in(adder_3_carry_out));
  adder adder_3 (.sum(out_5[5]), .carry_out(adder_3_carry_out), .a(a[5]), .b(in_2[5]), .carry_in(adder_4_carry_out));
  adder adder_4 (.sum(out_5[4]), .carry_out(adder_4_carry_out), .a(a[4]), .b(in_2[4]), .carry_in(adder_5_carry_out));
  adder adder_5 (.sum(out_5[3]), .carry_out(adder_5_carry_out), .a(a[3]), .b(in_2[3]), .carry_in(adder_6_carry_out));
  adder adder_6 (.sum(out_5[2]), .carry_out(adder_6_carry_out), .a(a[2]), .b(in_2[2]), .carry_in(adder_7_carry_out));
  adder adder_7 (.sum(out_5[1]), .carry_out(adder_7_carry_out), .a(a[1]), .b(in_2[1]), .carry_in(adder_8_carry_out));
  adder adder_8 (.sum(out_5[0]), .carry_out(adder_8_carry_out), .a(a[0]), .b(in_2[0]), .carry_in(in_3));
endmodule

module IAR (
  input  [7:0] i,
  input  s,
  input  e,
  output [7:0] o
);

  wire [7:0] n8_bit_memory_1_o;

  _8_bit_memory u_8_bit_memory_1 (.i(i), .s(s), .o(n8_bit_memory_1_o));
  Enabler enabler_1 (.i(n8_bit_memory_1_o), .e(e), .o(o));
endmodule
